// Logisim project JAM1.circ as structural Verilog: 6 circuits, main circuit main
module main (
);

  wire address_register_1_addr_assert_led, address_register_1_counter_0_led,
       address_register_1_counter_1_led, address_register_1_counter_2_led, address_register_1_counter_3_led,
       address_register_1_counter_4_led, address_register_1_counter_5_led, address_register_1_counter_6_led,
       address_register_1_counter_7_led, address_register_1_counter_8_led, address_register_1_counter_9_led,
       address_register_1_counter_10_led, address_register_1_counter_11_led,
       address_register_1_counter_12_led, address_register_1_counter_13_led,
       address_register_1_counter_14_led, address_register_1_counter_15_led, address_register_1_dec_led,
       address_register_1_inc_led, address_register_1_load_led, address_register_1_xfer_assert_led,
       address_register_2_addr_assert_led, address_register_2_counter_0_led,
       address_register_2_counter_1_led, address_register_2_counter_2_led, address_register_2_counter_3_led,
       address_register_2_counter_4_led, address_register_2_counter_5_led, address_register_2_counter_6_led,
       address_register_2_counter_7_led, address_register_2_counter_8_led, address_register_2_counter_9_led,
       address_register_2_counter_10_led, address_register_2_counter_11_led,
       address_register_2_counter_12_led, address_register_2_counter_13_led,
       address_register_2_counter_14_led, address_register_2_counter_15_led, address_register_2_dec_led,
       address_register_2_inc_led, address_register_2_load_led, address_register_2_xfer_assert_led,
       address_register_3_addr_assert_led, address_register_3_counter_0_led,
       address_register_3_counter_1_led, address_register_3_counter_2_led, address_register_3_counter_3_led,
       address_register_3_counter_4_led, address_register_3_counter_5_led, address_register_3_counter_6_led,
       address_register_3_counter_7_led, address_register_3_counter_8_led, address_register_3_counter_9_led,
       address_register_3_counter_10_led, address_register_3_counter_11_led,
       address_register_3_counter_12_led, address_register_3_counter_13_led,
       address_register_3_counter_14_led, address_register_3_counter_15_led, address_register_3_dec_led,
       address_register_3_inc_led, address_register_3_load_led, address_register_3_xfer_assert_led,
       address_register_4_addr_assert_led, address_register_4_counter_0_led,
       address_register_4_counter_1_led, address_register_4_counter_2_led, address_register_4_counter_3_led,
       address_register_4_counter_4_led, address_register_4_counter_5_led, address_register_4_counter_6_led,
       address_register_4_counter_7_led, address_register_4_counter_8_led, address_register_4_counter_9_led,
       address_register_4_counter_10_led, address_register_4_counter_11_led,
       address_register_4_counter_12_led, address_register_4_counter_13_led,
       address_register_4_counter_14_led, address_register_4_counter_15_led, address_register_4_dec_led,
       address_register_4_inc_led, address_register_4_load_led, address_register_4_xfer_assert_led,
       address_register_5_addr_assert_led, address_register_5_counter_0_led,
       address_register_5_counter_1_led, address_register_5_counter_2_led, address_register_5_counter_3_led,
       address_register_5_counter_4_led, address_register_5_counter_5_led, address_register_5_counter_6_led,
       address_register_5_counter_7_led, address_register_5_counter_8_led, address_register_5_counter_9_led,
       address_register_5_counter_10_led, address_register_5_counter_11_led,
       address_register_5_counter_12_led, address_register_5_counter_13_led,
       address_register_5_counter_14_led, address_register_5_counter_15_led, address_register_5_dec_led,
       address_register_5_inc_led, address_register_5_load_led, address_register_5_xfer_assert_led,
       ALU_ASSERT, and_1_out, buffer_1_out, bus_control_1_a_data_assert, bus_control_1_a_lhs_assert,
       bus_control_1_a_load, bus_control_1_a_rhs_assert, bus_control_1_a_rst, bus_control_1_b_data_assert,
       bus_control_1_b_lhs_assert, bus_control_1_b_load, bus_control_1_b_rhs_assert, bus_control_1_b_rst,
       bus_control_1_c_data_asssert, bus_control_1_c_lhs_assert, bus_control_1_c_load,
       bus_control_1_c_rhs_assert, bus_control_1_c_rst, bus_control_1_const_assert,
       bus_control_1_const_data_load, bus_control_1_const_mem_load, bus_control_1_const_rst,
       bus_control_1_d_data_assert, bus_control_1_d_lhs_assert, bus_control_1_d_load,
       bus_control_1_d_rhs_assert, bus_control_1_d_rst, bus_control_1_di_addr_assert, bus_control_1_di_clk,
       bus_control_1_di_dec, bus_control_1_di_inc, bus_control_1_di_load, bus_control_1_di_rst,
       bus_control_1_di_xfer_assert, bus_control_1_pc_addr_assert, bus_control_1_pc_clk,
       bus_control_1_pc_dec, bus_control_1_pc_inc, bus_control_1_pc_load, bus_control_1_pc_rst,
       bus_control_1_pc_xfer_assert, bus_control_1_ra_addr_assert, bus_control_1_ra_clk,
       bus_control_1_ra_dec, bus_control_1_ra_inc, bus_control_1_ra_load, bus_control_1_ra_rst,
       bus_control_1_ra_xfer_assert, bus_control_1_si_addr_assert, bus_control_1_si_clk,
       bus_control_1_si_dec, bus_control_1_si_inc, bus_control_1_si_load, bus_control_1_si_rst,
       bus_control_1_si_xfer_assert, bus_control_1_sp_addr_assert, bus_control_1_sp_clk,
       bus_control_1_sp_dec, bus_control_1_sp_inc, bus_control_1_sp_load, bus_control_1_sp_rst,
       bus_control_1_sp_xfer_assert, bus_control_1_th_assert, bus_control_1_th_load, bus_control_1_tl_assert,
       bus_control_1_tl_load, bus_control_1_tx_addr_assert, bus_control_1_tx_load,
       bus_control_1_tx_mode_assert, bus_control_1_tx_rst, bus_control_1_tx_xfer_assert, BUS_REQUEST, CLK,
       constant_register_1_data_assert_led, constant_register_1_databus_0_led,
       constant_register_1_databus_1_led, constant_register_1_databus_2_led,
       constant_register_1_databus_3_led, constant_register_1_databus_4_led,
       constant_register_1_databus_5_led, constant_register_1_databus_6_led,
       constant_register_1_databus_7_led, constant_register_1_mem_bus_load_led,
       constant_register_1_register_1_led, constant_register_1_register_2_led,
       constant_register_1_register_3_led, constant_register_1_register_4_led,
       constant_register_1_register_5_led, constant_register_1_register_6_led,
       constant_register_1_register_7_led, constant_register_1_regsiter_0_led, controlled_buffer_7_out,
       controlled_buffer_8_out, data_register_1_data_assert_led, data_register_1_lhs_assert_led,
       data_register_1_load_led, data_register_1_register_1_led, data_register_1_register_2_led,
       data_register_1_register_3_led, data_register_1_register_4_led, data_register_1_register_5_led,
       data_register_1_register_6_led, data_register_1_register_7_led, data_register_1_regsiter_0_led,
       data_register_1_rhs_assert_led, data_register_2_data_assert_led, data_register_2_lhs_assert_led,
       data_register_2_load_led, data_register_2_register_1_led, data_register_2_register_2_led,
       data_register_2_register_3_led, data_register_2_register_4_led, data_register_2_register_5_led,
       data_register_2_register_6_led, data_register_2_register_7_led, data_register_2_regsiter_0_led,
       data_register_2_rhs_assert_led, data_register_3_data_assert_led, data_register_3_lhs_assert_led,
       data_register_3_load_led, data_register_3_register_1_led, data_register_3_register_2_led,
       data_register_3_register_3_led, data_register_3_register_4_led, data_register_3_register_5_led,
       data_register_3_register_6_led, data_register_3_register_7_led, data_register_3_regsiter_0_led,
       data_register_3_rhs_assert_led, data_register_4_data_assert_led, data_register_4_lhs_assert_led,
       data_register_4_load_led, data_register_4_register_1_led, data_register_4_register_2_led,
       data_register_4_register_3_led, data_register_4_register_4_led, data_register_4_register_5_led,
       data_register_4_register_6_led, data_register_4_register_7_led, data_register_4_regsiter_0_led,
       data_register_4_rhs_assert_led, DATA_TO_MEM_ASSERT, ICLK, LCD_LOAD, ledbar_22_p2, MEM_LOAD,
       multiplexer_8_out, multiplexer_12_out, NO_FETCH, nor_1_out, nor_3_out, nor_4_out, not_2_out,
       not_3_out, not_4_out, or_1_out, or_2_out, or_3_out, PC_RA_FLIP, por_1_out, register_11_q, RST,
       RST_BUTTON, transfer_register_1_register_1_led, transfer_register_1_register_2_led,
       transfer_register_1_register_3_led, transfer_register_1_register_4_led,
       transfer_register_1_register_5_led, transfer_register_1_register_6_led,
       transfer_register_1_register_7_led, transfer_register_1_register_8_led,
       transfer_register_1_register_9_led, transfer_register_1_register_10_led,
       transfer_register_1_register_11_led, transfer_register_1_register_12_led,
       transfer_register_1_register_13_led, transfer_register_1_register_14_led,
       transfer_register_1_register_15_led, transfer_register_1_regsiter_0_led,
       transfer_register_1_th_assert_led, transfer_register_1_th_load_led, transfer_register_1_tl_assert_led,
       transfer_register_1_tl_load_led, transfer_register_1_tx_addr_assert_led,
       transfer_register_1_tx_load_led, transfer_register_1_tx_xfer_assert_led, xor_1_out, xor_2_out;
  wire [1:0] INC_CONTROL, LHS_BUS_ASSERT_CONTROL, register_3_q, RHS_BUS_ASSERT_CONTROL;
  wire [2:0] ADDR_ASSERT_CONTROL, XFER_ASSERT_CONTROL;
  wire [3:0] ALU_CONTROL, bus_control_1_mem_control, DATA_BUS_ASSERT_CONTROL, DATA_BUS_LOAD_CONTROL,
       DEC_XFER_LOAD_CONTROL, multiplexer_10_out, multiplexer_11_out;
  wire [3:3] register_7_q;
  wire [4:0] ALU_FLAGS, bus_control_1_device_load;
  wire [6:0] adder_1_out;
  wire [7:0] ALU_LHS_BUS, ALU_RHS_BUS, controlled_buffer_1_out, controlled_buffer_6_out, DATA_BUS, MEM_BUS,
       multiplexer_9_out, ram_1_dout, register_1_q, register_2_q, register_5_q, register_6_q, rom_1_data,
       rom_2_data, rom_3_data, rom_4_data, rom_5_data, rom_6_data;
  wire [13:13] multiplexer_3_out;
  wire [15:0] ADDR_BUS, address_register_1_xfer_bus_out;

  // LedBar #(.inputtype("row"), .matrixcols(16)) ledbar_1: pin names not known; wires that end beside it: ADDR_BUS
  ROM #(.addrWidth(15)) rom_1 (.addr(ADDR_BUS[14:0]), .data(rom_1_data));
  POR por_1 (.out(por_1_out));
  LedBar #(.matrixcols(16)) ledbar_2 (
    .led0(address_register_1_counter_15_led), .led1(address_register_1_counter_14_led),
    .led2(address_register_1_counter_13_led), .led3(address_register_1_counter_12_led),
    .led4(address_register_1_counter_11_led), .led5(address_register_1_counter_10_led),
    .led6(address_register_1_counter_9_led), .led7(address_register_1_counter_8_led),
    .led8(address_register_1_counter_7_led), .led9(address_register_1_counter_6_led),
    .led10(address_register_1_counter_5_led), .led11(address_register_1_counter_4_led),
    .led12(address_register_1_counter_3_led), .led13(address_register_1_counter_2_led),
    .led14(address_register_1_counter_1_led), .led15(address_register_1_counter_0_led));
  LedBar #(.matrixcols(16)) ledbar_3 (
    .led0(address_register_2_counter_15_led), .led1(address_register_2_counter_14_led),
    .led2(address_register_2_counter_13_led), .led3(address_register_2_counter_12_led),
    .led4(address_register_2_counter_11_led), .led5(address_register_2_counter_10_led),
    .led6(address_register_2_counter_9_led), .led7(address_register_2_counter_8_led),
    .led8(address_register_2_counter_7_led), .led9(address_register_2_counter_6_led),
    .led10(address_register_2_counter_5_led), .led11(address_register_2_counter_4_led),
    .led12(address_register_2_counter_3_led), .led13(address_register_2_counter_2_led),
    .led14(address_register_2_counter_1_led), .led15(address_register_2_counter_0_led));
  LedBar #(.matrixcols(16)) ledbar_4 (
    .led0(address_register_3_counter_15_led), .led1(address_register_3_counter_14_led),
    .led2(address_register_3_counter_13_led), .led3(address_register_3_counter_12_led),
    .led4(address_register_3_counter_11_led), .led5(address_register_3_counter_10_led),
    .led6(address_register_3_counter_9_led), .led7(address_register_3_counter_8_led),
    .led8(address_register_3_counter_7_led), .led9(address_register_3_counter_6_led),
    .led10(address_register_3_counter_5_led), .led11(address_register_3_counter_4_led),
    .led12(address_register_3_counter_3_led), .led13(address_register_3_counter_2_led),
    .led14(address_register_3_counter_1_led), .led15(address_register_3_counter_0_led));
  LedBar #(.matrixcols(16)) ledbar_5 (
    .led0(address_register_4_counter_15_led), .led1(address_register_4_counter_14_led),
    .led2(address_register_4_counter_13_led), .led3(address_register_4_counter_12_led),
    .led4(address_register_4_counter_11_led), .led5(address_register_4_counter_10_led),
    .led6(address_register_4_counter_9_led), .led7(address_register_4_counter_8_led),
    .led8(address_register_4_counter_7_led), .led9(address_register_4_counter_6_led),
    .led10(address_register_4_counter_5_led), .led11(address_register_4_counter_4_led),
    .led12(address_register_4_counter_3_led), .led13(address_register_4_counter_2_led),
    .led14(address_register_4_counter_1_led), .led15(address_register_4_counter_0_led));
  LedBar #(.matrixcols(16)) ledbar_6 (
    .led0(address_register_5_counter_15_led), .led1(address_register_5_counter_14_led),
    .led2(address_register_5_counter_13_led), .led3(address_register_5_counter_12_led),
    .led4(address_register_5_counter_11_led), .led5(address_register_5_counter_10_led),
    .led6(address_register_5_counter_9_led), .led7(address_register_5_counter_8_led),
    .led8(address_register_5_counter_7_led), .led9(address_register_5_counter_6_led),
    .led10(address_register_5_counter_5_led), .led11(address_register_5_counter_4_led),
    .led12(address_register_5_counter_3_led), .led13(address_register_5_counter_2_led),
    .led14(address_register_5_counter_1_led), .led15(address_register_5_counter_0_led));
  LedBar ledbar_7 (
    .led0(transfer_register_1_register_15_led), .led1(transfer_register_1_register_14_led),
    .led2(transfer_register_1_register_13_led), .led3(transfer_register_1_register_12_led),
    .led4(transfer_register_1_register_11_led), .led5(transfer_register_1_register_10_led),
    .led6(transfer_register_1_register_9_led), .led7(transfer_register_1_register_8_led));
  or or_1 (or_1_out, por_1_out, RST_BUTTON);
  LED led_1 (.in(address_register_1_inc_led));
  LED led_2 (.in(address_register_1_addr_assert_led));
  LED led_3 (.in(address_register_1_dec_led));
  LED led_4 (.in(address_register_1_xfer_assert_led));
  LED led_5 (.in(address_register_2_inc_led));
  LED led_6 (.in(address_register_2_addr_assert_led));
  LED led_7 (.in(address_register_2_dec_led));
  LED led_8 (.in(address_register_2_xfer_assert_led));
  LED led_9 (.in(address_register_3_inc_led));
  LED led_10 (.in(address_register_3_addr_assert_led));
  LED led_11 (.in(address_register_3_dec_led));
  LED led_12 (.in(address_register_3_xfer_assert_led));
  LED led_13 (.in(address_register_4_inc_led));
  LED led_14 (.in(address_register_4_addr_assert_led));
  LED led_15 (.in(address_register_4_dec_led));
  LED led_16 (.in(address_register_4_xfer_assert_led));
  LED led_17 (.in(address_register_5_inc_led));
  LED led_18 (.in(address_register_5_addr_assert_led));
  LED led_19 (.in(address_register_5_dec_led));
  LED led_20 (.in(address_register_5_xfer_assert_led));
  LED led_21 (.in(transfer_register_1_th_assert_led));
  LED led_22 (.in(transfer_register_1_th_load_led));
  LED led_23 (.in(transfer_register_1_tl_assert_led));
  LED led_24 (.in(transfer_register_1_tl_load_led));
  nor nor_1 (nor_1_out, or_1_out, RST);
  nor nor_2 (RST, nor_1_out, CLK);
  Clock clock_1 (.out(CLK));
  LED led_25 (.in(address_register_1_load_led));
  LED led_26 (.in(address_register_2_load_led));
  LED led_27 (.in(address_register_3_load_led));
  LED led_28 (.in(address_register_4_load_led));
  LED led_29 (.in(address_register_5_load_led));
  LedBar ledbar_8 (
    .led0(transfer_register_1_register_7_led), .led1(transfer_register_1_register_6_led),
    .led2(transfer_register_1_register_5_led), .led3(transfer_register_1_register_4_led),
    .led4(transfer_register_1_register_3_led), .led5(transfer_register_1_register_2_led),
    .led6(transfer_register_1_register_1_led), .led7(transfer_register_1_regsiter_0_led));
  LED led_30 (.in(transfer_register_1_tx_xfer_assert_led));
  LED led_31 (.in(transfer_register_1_tx_addr_assert_led));
  not not_1 (ICLK, CLK);
  Address_Register address_register_1 (
    .LOAD(bus_control_1_pc_load), .INC(bus_control_1_pc_inc), .DEC(bus_control_1_pc_dec),
    .RST_IN(bus_control_1_pc_rst), .CLK_IN(bus_control_1_pc_clk), .XFER_ASSERT(bus_control_1_pc_xfer_assert),
    .ADDR_ASSERT(bus_control_1_pc_addr_assert), .XFER_BUS_IN(address_register_1_xfer_bus_out),
    .LOAD_LED(address_register_1_load_led), .INC_LED(address_register_1_inc_led),
    .DEC_LED(address_register_1_dec_led), .Counter_0_LED(address_register_1_counter_0_led),
    .Counter_1_LED(address_register_1_counter_1_led), .Counter_2_LED(address_register_1_counter_2_led),
    .Counter_3_LED(address_register_1_counter_3_led), .Counter_4_LED(address_register_1_counter_4_led),
    .Counter_5_LED(address_register_1_counter_5_led), .Counter_6_LED(address_register_1_counter_6_led),
    .Counter_7_LED(address_register_1_counter_7_led), .Counter_8_LED(address_register_1_counter_8_led),
    .Counter_9_LED(address_register_1_counter_9_led), .Counter_10_LED(address_register_1_counter_10_led),
    .Counter_11_LED(address_register_1_counter_11_led), .Counter_12_LED(address_register_1_counter_12_led),
    .Counter_13_LED(address_register_1_counter_13_led), .Counter_14_LED(address_register_1_counter_14_led),
    .Counter_15_LED(address_register_1_counter_15_led), .XFER_ASSERT_LED(address_register_1_xfer_assert_led),
    .ADDR_ASSERT_LED(address_register_1_addr_assert_led), .XFER_BUS_OUT(address_register_1_xfer_bus_out),
    .ADDR_BUS_OUT(ADDR_BUS));
  Address_Register address_register_2 (
    .LOAD(bus_control_1_ra_load), .INC(bus_control_1_ra_inc), .DEC(bus_control_1_ra_dec),
    .RST_IN(bus_control_1_ra_rst), .CLK_IN(bus_control_1_ra_clk), .XFER_ASSERT(bus_control_1_ra_xfer_assert),
    .ADDR_ASSERT(bus_control_1_ra_addr_assert), .XFER_BUS_IN(address_register_1_xfer_bus_out),
    .LOAD_LED(address_register_2_load_led), .INC_LED(address_register_2_inc_led),
    .DEC_LED(address_register_2_dec_led), .Counter_0_LED(address_register_2_counter_0_led),
    .Counter_1_LED(address_register_2_counter_1_led), .Counter_2_LED(address_register_2_counter_2_led),
    .Counter_3_LED(address_register_2_counter_3_led), .Counter_4_LED(address_register_2_counter_4_led),
    .Counter_5_LED(address_register_2_counter_5_led), .Counter_6_LED(address_register_2_counter_6_led),
    .Counter_7_LED(address_register_2_counter_7_led), .Counter_8_LED(address_register_2_counter_8_led),
    .Counter_9_LED(address_register_2_counter_9_led), .Counter_10_LED(address_register_2_counter_10_led),
    .Counter_11_LED(address_register_2_counter_11_led), .Counter_12_LED(address_register_2_counter_12_led),
    .Counter_13_LED(address_register_2_counter_13_led), .Counter_14_LED(address_register_2_counter_14_led),
    .Counter_15_LED(address_register_2_counter_15_led), .XFER_ASSERT_LED(address_register_2_xfer_assert_led),
    .ADDR_ASSERT_LED(address_register_2_addr_assert_led), .XFER_BUS_OUT(address_register_1_xfer_bus_out),
    .ADDR_BUS_OUT(ADDR_BUS));
  Address_Register address_register_3 (
    .LOAD(bus_control_1_sp_load), .INC(bus_control_1_sp_inc), .DEC(bus_control_1_sp_dec),
    .RST_IN(bus_control_1_sp_rst), .CLK_IN(bus_control_1_sp_clk), .XFER_ASSERT(bus_control_1_sp_xfer_assert),
    .ADDR_ASSERT(bus_control_1_sp_addr_assert), .XFER_BUS_IN(address_register_1_xfer_bus_out),
    .LOAD_LED(address_register_3_load_led), .INC_LED(address_register_3_inc_led),
    .DEC_LED(address_register_3_dec_led), .Counter_0_LED(address_register_3_counter_0_led),
    .Counter_1_LED(address_register_3_counter_1_led), .Counter_2_LED(address_register_3_counter_2_led),
    .Counter_3_LED(address_register_3_counter_3_led), .Counter_4_LED(address_register_3_counter_4_led),
    .Counter_5_LED(address_register_3_counter_5_led), .Counter_6_LED(address_register_3_counter_6_led),
    .Counter_7_LED(address_register_3_counter_7_led), .Counter_8_LED(address_register_3_counter_8_led),
    .Counter_9_LED(address_register_3_counter_9_led), .Counter_10_LED(address_register_3_counter_10_led),
    .Counter_11_LED(address_register_3_counter_11_led), .Counter_12_LED(address_register_3_counter_12_led),
    .Counter_13_LED(address_register_3_counter_13_led), .Counter_14_LED(address_register_3_counter_14_led),
    .Counter_15_LED(address_register_3_counter_15_led), .XFER_ASSERT_LED(address_register_3_xfer_assert_led),
    .ADDR_ASSERT_LED(address_register_3_addr_assert_led), .XFER_BUS_OUT(address_register_1_xfer_bus_out),
    .ADDR_BUS_OUT(ADDR_BUS));
  Address_Register address_register_4 (
    .LOAD(bus_control_1_si_load), .INC(bus_control_1_si_inc), .DEC(bus_control_1_si_dec),
    .RST_IN(bus_control_1_si_rst), .CLK_IN(bus_control_1_si_clk), .XFER_ASSERT(bus_control_1_si_xfer_assert),
    .ADDR_ASSERT(bus_control_1_si_addr_assert), .XFER_BUS_IN(address_register_1_xfer_bus_out),
    .LOAD_LED(address_register_4_load_led), .INC_LED(address_register_4_inc_led),
    .DEC_LED(address_register_4_dec_led), .Counter_0_LED(address_register_4_counter_0_led),
    .Counter_1_LED(address_register_4_counter_1_led), .Counter_2_LED(address_register_4_counter_2_led),
    .Counter_3_LED(address_register_4_counter_3_led), .Counter_4_LED(address_register_4_counter_4_led),
    .Counter_5_LED(address_register_4_counter_5_led), .Counter_6_LED(address_register_4_counter_6_led),
    .Counter_7_LED(address_register_4_counter_7_led), .Counter_8_LED(address_register_4_counter_8_led),
    .Counter_9_LED(address_register_4_counter_9_led), .Counter_10_LED(address_register_4_counter_10_led),
    .Counter_11_LED(address_register_4_counter_11_led), .Counter_12_LED(address_register_4_counter_12_led),
    .Counter_13_LED(address_register_4_counter_13_led), .Counter_14_LED(address_register_4_counter_14_led),
    .Counter_15_LED(address_register_4_counter_15_led), .XFER_ASSERT_LED(address_register_4_xfer_assert_led),
    .ADDR_ASSERT_LED(address_register_4_addr_assert_led), .XFER_BUS_OUT(address_register_1_xfer_bus_out),
    .ADDR_BUS_OUT(ADDR_BUS));
  Address_Register address_register_5 (
    .LOAD(bus_control_1_di_load), .INC(bus_control_1_di_inc), .DEC(bus_control_1_di_dec),
    .RST_IN(bus_control_1_di_rst), .CLK_IN(bus_control_1_di_clk), .XFER_ASSERT(bus_control_1_di_xfer_assert),
    .ADDR_ASSERT(bus_control_1_di_addr_assert), .XFER_BUS_IN(address_register_1_xfer_bus_out),
    .LOAD_LED(address_register_5_load_led), .INC_LED(address_register_5_inc_led),
    .DEC_LED(address_register_5_dec_led), .Counter_0_LED(address_register_5_counter_0_led),
    .Counter_1_LED(address_register_5_counter_1_led), .Counter_2_LED(address_register_5_counter_2_led),
    .Counter_3_LED(address_register_5_counter_3_led), .Counter_4_LED(address_register_5_counter_4_led),
    .Counter_5_LED(address_register_5_counter_5_led), .Counter_6_LED(address_register_5_counter_6_led),
    .Counter_7_LED(address_register_5_counter_7_led), .Counter_8_LED(address_register_5_counter_8_led),
    .Counter_9_LED(address_register_5_counter_9_led), .Counter_10_LED(address_register_5_counter_10_led),
    .Counter_11_LED(address_register_5_counter_11_led), .Counter_12_LED(address_register_5_counter_12_led),
    .Counter_13_LED(address_register_5_counter_13_led), .Counter_14_LED(address_register_5_counter_14_led),
    .Counter_15_LED(address_register_5_counter_15_led), .XFER_ASSERT_LED(address_register_5_xfer_assert_led),
    .ADDR_ASSERT_LED(address_register_5_addr_assert_led), .XFER_BUS_OUT(address_register_1_xfer_bus_out),
    .ADDR_BUS_OUT(ADDR_BUS));
  LED led_32 (.in(transfer_register_1_tx_load_led));
  not not_2 (not_2_out, ADDR_BUS[15]);
  assign controlled_buffer_1_out = not_2_out ? rom_1_data : 8'bz;  // Controlled_Buffer controlled_buffer_1
  Bus_Control bus_control_1 (
    .CONTROL_IN({DATA_BUS_ASSERT_CONTROL, DATA_BUS_LOAD_CONTROL, LHS_BUS_ASSERT_CONTROL, RHS_BUS_ASSERT_CONTROL, ADDR_ASSERT_CONTROL, XFER_ASSERT_CONTROL, DEC_XFER_LOAD_CONTROL, INC_CONTROL, BUS_REQUEST, PC_RA_FLIP}),
    .CLK_IN(CLK), .RST_IN(RST),
    .MEM_CONTROL({bus_control_1_mem_control[3], MEM_LOAD, DATA_TO_MEM_ASSERT, bus_control_1_mem_control[0]}),
    .CONST_MEM_LOAD(bus_control_1_const_mem_load), .PC_DEC(bus_control_1_pc_dec),
    .RA_DEC(bus_control_1_ra_dec), .SP_DEC(bus_control_1_sp_dec), .SI_DEC(bus_control_1_si_dec),
    .DI_DEC(bus_control_1_di_dec), .PC_XFER_ASSERT(bus_control_1_pc_xfer_assert),
    .RA_XFER_ASSERT(bus_control_1_ra_xfer_assert), .SP_XFER_ASSERT(bus_control_1_sp_xfer_assert),
    .SI_XFER_ASSERT(bus_control_1_si_xfer_assert), .DI_XFER_ASSERT(bus_control_1_di_xfer_assert),
    .TX_XFER_ASSERT(bus_control_1_tx_xfer_assert), .TX_MODE_ASSERT(bus_control_1_tx_mode_assert),
    .PC_LOAD(bus_control_1_pc_load), .RA_LOAD(bus_control_1_ra_load), .SP_LOAD(bus_control_1_sp_load),
    .SI_LOAD(bus_control_1_si_load), .DI_LOAD(bus_control_1_di_load), .TX_LOAD(bus_control_1_tx_load),
    .PC_ADDR_ASSERT(bus_control_1_pc_addr_assert), .RA_ADDR_ASSERT(bus_control_1_ra_addr_assert),
    .SP_ADDR_ASSERT(bus_control_1_sp_addr_assert), .SI_ADDR_ASSERT(bus_control_1_si_addr_assert),
    .DI_ADDR_ASSERT(bus_control_1_di_addr_assert), .TX_ADDR_ASSERT(bus_control_1_tx_addr_assert),
    .SP_INC(bus_control_1_sp_inc), .SI_INC(bus_control_1_si_inc), .DI_INC(bus_control_1_di_inc),
    .A_LHS_ASSERT(bus_control_1_a_lhs_assert), .B_LHS_ASSERT(bus_control_1_b_lhs_assert),
    .C_LHS_ASSERT(bus_control_1_c_lhs_assert), .D_LHS_ASSERT(bus_control_1_d_lhs_assert),
    .PC_INC(bus_control_1_pc_inc), .RA_INC(bus_control_1_ra_inc), .A_RHS_ASSERT(bus_control_1_a_rhs_assert),
    .B_RHS_ASSERT(bus_control_1_b_rhs_assert), .C_RHS_ASSERT(bus_control_1_c_rhs_assert),
    .D_RHS_ASSERT(bus_control_1_d_rhs_assert), .DEVICE_LOAD({LCD_LOAD, bus_control_1_device_load}),
    .PC_CLK(bus_control_1_pc_clk), .RA_CLK(bus_control_1_ra_clk), .SP_CLK(bus_control_1_sp_clk),
    .SI_CLK(bus_control_1_si_clk), .DI_CLK(bus_control_1_di_clk), .CONST_ASSERT(bus_control_1_const_assert),
    .TL_ASSERT(bus_control_1_tl_assert), .TH_ASSERT(bus_control_1_th_assert), .ALU_ASSERT(ALU_ASSERT),
    .A_LOAD(bus_control_1_a_load), .B_LOAD(bus_control_1_b_load), .C_LOAD(bus_control_1_c_load),
    .D_LOAD(bus_control_1_d_load), .CONST_DATA_LOAD(bus_control_1_const_data_load),
    .TL_LOAD(bus_control_1_tl_load), .TH_LOAD(bus_control_1_th_load),
    .A_DATA_ASSERT(bus_control_1_a_data_assert), .B_DATA_ASSERT(bus_control_1_b_data_assert),
    .C_DATA_ASSSERT(bus_control_1_c_data_asssert), .D_DATA_ASSERT(bus_control_1_d_data_assert),
    .A_RST(bus_control_1_a_rst), .B_RST(bus_control_1_b_rst), .C_RST(bus_control_1_c_rst),
    .D_RST(bus_control_1_d_rst), .CONST_RST(bus_control_1_const_rst), .PC_RST(bus_control_1_pc_rst),
    .RA_RST(bus_control_1_ra_rst), .SP_RST(bus_control_1_sp_rst), .SI_RST(bus_control_1_si_rst),
    .DI_RST(bus_control_1_di_rst), .TX_RST(bus_control_1_tx_rst));  // open: DEVICE_ASSERT
  Transfer_Register transfer_register_1 (
    .TX_XFER_ASSERT(bus_control_1_tx_xfer_assert), .TX_ADDR_ASSERT(bus_control_1_tx_addr_assert),
    .XFER_BUS_IN(address_register_1_xfer_bus_out), .DATA_BUS_IN(DATA_BUS), .TX_LOAD(bus_control_1_tx_load),
    .TL_LOAD(bus_control_1_tl_load), .TH_LOAD(bus_control_1_th_load), .RST_IN(bus_control_1_tx_rst),
    .TL_ASSERT(bus_control_1_tl_assert), .TH_ASSERT(bus_control_1_th_assert),
    .TX_XFER_ASSERT_LED(transfer_register_1_tx_xfer_assert_led),
    .TX_ADDR_ASSERT_LED(transfer_register_1_tx_addr_assert_led),
    .XFER_BUS_OUT(address_register_1_xfer_bus_out), .ADDR_BUS_OUT(ADDR_BUS),
    .TX_LOAD_LED(transfer_register_1_tx_load_led), .TL_LOAD_LED(transfer_register_1_tl_load_led),
    .TH_LOAD_LED(transfer_register_1_th_load_led), .Register_3_LED(transfer_register_1_register_3_led),
    .Register_4_LED(transfer_register_1_register_4_led), .Register_5_LED(transfer_register_1_register_5_led),
    .Register_6_LED(transfer_register_1_register_6_led), .Register_7_LED(transfer_register_1_register_7_led),
    .TL_ASSERT_LED(transfer_register_1_tl_assert_led), .Regsiter_0_LED(transfer_register_1_regsiter_0_led),
    .Register_1_LED(transfer_register_1_register_1_led), .Register_2_LED(transfer_register_1_register_2_led),
    .Register_8_LED(transfer_register_1_register_8_led), .Register_9_LED(transfer_register_1_register_9_led),
    .Register_10_LED(transfer_register_1_register_10_led),
    .Register_11_LED(transfer_register_1_register_11_led),
    .Register_12_LED(transfer_register_1_register_12_led),
    .Register_13_LED(transfer_register_1_register_13_led),
    .Register_14_LED(transfer_register_1_register_14_led),
    .Register_15_LED(transfer_register_1_register_15_led), .TH_ASSERT_LED(transfer_register_1_th_assert_led),
    .DATA_BUS_OUT(DATA_BUS));
  RAM #(.addrWidth(15), .asyncread("true"), .clearpin("true")) ram_1 (
    .addr(ADDR_BUS[14:0]), .we(1'b1), .oe(1'b1), .clk(MEM_LOAD), .din(MEM_BUS), .dout(ram_1_dout), .clr(RST));
  Data_Register data_register_1 (
    .LOAD(bus_control_1_a_load), .RST_IN(bus_control_1_a_rst), .DATA_ASSERT(bus_control_1_a_data_assert),
    .LHS_ASSERT(bus_control_1_a_lhs_assert), .RHS_ASSERT(bus_control_1_a_rhs_assert), .DATA_BUS_IN(DATA_BUS),
    .LOAD_LED(data_register_1_load_led), .Regsiter_0_LED(data_register_1_regsiter_0_led),
    .Register_1_LED(data_register_1_register_1_led), .Register_2_LED(data_register_1_register_2_led),
    .Register_3_LED(data_register_1_register_3_led), .Register_4_LED(data_register_1_register_4_led),
    .Register_5_LED(data_register_1_register_5_led), .Register_6_LED(data_register_1_register_6_led),
    .Register_7_LED(data_register_1_register_7_led), .DATA_ASSERT_LED(data_register_1_data_assert_led),
    .LHS_ASSERT_LED(data_register_1_lhs_assert_led), .RHS_ASSERT_LED(data_register_1_rhs_assert_led),
    .DATA_BUS_OUT(DATA_BUS), .LHS_BUS_OUT(ALU_LHS_BUS), .RHS_BUS_OUT(ALU_RHS_BUS));
  LedBar ledbar_9 (
    .led0(data_register_1_register_7_led), .led1(data_register_1_register_6_led),
    .led2(data_register_1_register_5_led), .led3(data_register_1_register_4_led),
    .led4(data_register_1_register_3_led), .led5(data_register_1_register_2_led),
    .led6(data_register_1_register_1_led), .led7(data_register_1_regsiter_0_led));
  LED led_33 (.in(data_register_1_lhs_assert_led));
  LED led_34 (.in(data_register_1_data_assert_led));
  Data_Register data_register_2 (
    .LOAD(bus_control_1_b_load), .RST_IN(bus_control_1_b_rst), .DATA_ASSERT(bus_control_1_b_data_assert),
    .LHS_ASSERT(bus_control_1_b_lhs_assert), .RHS_ASSERT(bus_control_1_b_rhs_assert), .DATA_BUS_IN(DATA_BUS),
    .LOAD_LED(data_register_2_load_led), .Regsiter_0_LED(data_register_2_regsiter_0_led),
    .Register_1_LED(data_register_2_register_1_led), .Register_2_LED(data_register_2_register_2_led),
    .Register_3_LED(data_register_2_register_3_led), .Register_4_LED(data_register_2_register_4_led),
    .Register_5_LED(data_register_2_register_5_led), .Register_6_LED(data_register_2_register_6_led),
    .Register_7_LED(data_register_2_register_7_led), .DATA_ASSERT_LED(data_register_2_data_assert_led),
    .LHS_ASSERT_LED(data_register_2_lhs_assert_led), .RHS_ASSERT_LED(data_register_2_rhs_assert_led),
    .DATA_BUS_OUT(DATA_BUS), .LHS_BUS_OUT(ALU_LHS_BUS), .RHS_BUS_OUT(ALU_RHS_BUS));
  LedBar ledbar_10 (
    .led0(data_register_2_register_7_led), .led1(data_register_2_register_6_led),
    .led2(data_register_2_register_5_led), .led3(data_register_2_register_4_led),
    .led4(data_register_2_register_3_led), .led5(data_register_2_register_2_led),
    .led6(data_register_2_register_1_led), .led7(data_register_2_regsiter_0_led));
  LED led_35 (.in(data_register_2_lhs_assert_led));
  LED led_36 (.in(data_register_2_data_assert_led));
  Data_Register data_register_3 (
    .LOAD(bus_control_1_c_load), .RST_IN(bus_control_1_c_rst), .DATA_ASSERT(bus_control_1_c_data_asssert),
    .LHS_ASSERT(bus_control_1_c_lhs_assert), .RHS_ASSERT(bus_control_1_c_rhs_assert), .DATA_BUS_IN(DATA_BUS),
    .LOAD_LED(data_register_3_load_led), .Regsiter_0_LED(data_register_3_regsiter_0_led),
    .Register_1_LED(data_register_3_register_1_led), .Register_2_LED(data_register_3_register_2_led),
    .Register_3_LED(data_register_3_register_3_led), .Register_4_LED(data_register_3_register_4_led),
    .Register_5_LED(data_register_3_register_5_led), .Register_6_LED(data_register_3_register_6_led),
    .Register_7_LED(data_register_3_register_7_led), .DATA_ASSERT_LED(data_register_3_data_assert_led),
    .LHS_ASSERT_LED(data_register_3_lhs_assert_led), .RHS_ASSERT_LED(data_register_3_rhs_assert_led),
    .DATA_BUS_OUT(DATA_BUS), .LHS_BUS_OUT(ALU_LHS_BUS), .RHS_BUS_OUT(ALU_RHS_BUS));
  LedBar ledbar_11 (
    .led0(data_register_3_register_7_led), .led1(data_register_3_register_6_led),
    .led2(data_register_3_register_5_led), .led3(data_register_3_register_4_led),
    .led4(data_register_3_register_3_led), .led5(data_register_3_register_2_led),
    .led6(data_register_3_register_1_led), .led7(data_register_3_regsiter_0_led));
  LED led_37 (.in(data_register_3_lhs_assert_led));
  LED led_38 (.in(data_register_3_data_assert_led));
  Data_Register data_register_4 (
    .LOAD(bus_control_1_d_load), .RST_IN(bus_control_1_d_rst), .DATA_ASSERT(bus_control_1_d_data_assert),
    .LHS_ASSERT(bus_control_1_d_lhs_assert), .RHS_ASSERT(bus_control_1_d_rhs_assert), .DATA_BUS_IN(DATA_BUS),
    .LOAD_LED(data_register_4_load_led), .Regsiter_0_LED(data_register_4_regsiter_0_led),
    .Register_1_LED(data_register_4_register_1_led), .Register_2_LED(data_register_4_register_2_led),
    .Register_3_LED(data_register_4_register_3_led), .Register_4_LED(data_register_4_register_4_led),
    .Register_5_LED(data_register_4_register_5_led), .Register_6_LED(data_register_4_register_6_led),
    .Register_7_LED(data_register_4_register_7_led), .DATA_ASSERT_LED(data_register_4_data_assert_led),
    .LHS_ASSERT_LED(data_register_4_lhs_assert_led), .RHS_ASSERT_LED(data_register_4_rhs_assert_led),
    .DATA_BUS_OUT(DATA_BUS), .LHS_BUS_OUT(ALU_LHS_BUS), .RHS_BUS_OUT(ALU_RHS_BUS));
  LedBar ledbar_12 (
    .led0(data_register_4_register_7_led), .led1(data_register_4_register_6_led),
    .led2(data_register_4_register_5_led), .led3(data_register_4_register_4_led),
    .led4(data_register_4_register_3_led), .led5(data_register_4_register_2_led),
    .led6(data_register_4_register_1_led), .led7(data_register_4_regsiter_0_led));
  LED led_39 (.in(data_register_4_lhs_assert_led));
  LED led_40 (.in(data_register_4_data_assert_led));
  LedBar ledbar_13 (
    .led0(constant_register_1_register_7_led), .led1(constant_register_1_register_6_led),
    .led2(constant_register_1_register_5_led), .led3(constant_register_1_register_4_led),
    .led4(constant_register_1_register_3_led), .led5(constant_register_1_register_2_led),
    .led6(constant_register_1_register_1_led), .led7(constant_register_1_regsiter_0_led));
  LED led_41 (.in(constant_register_1_data_assert_led));
  LED led_42 (.in(constant_register_1_mem_bus_load_led));
  Constant_Register constant_register_1 (
    .DATA_BUS_IN(DATA_BUS), .MEM_BUS_LOAD(bus_control_1_const_mem_load),
    .DATA_BUS_LOAD(bus_control_1_const_data_load), .MEM_BUS_IN(MEM_BUS), .RST_IN(bus_control_1_const_rst),
    .DATA_ASSERT(bus_control_1_const_assert), .DataBus_0_LED(constant_register_1_databus_0_led),
    .DataBus_1_LED(constant_register_1_databus_1_led), .DataBus_2_LED(constant_register_1_databus_2_led),
    .DataBus_3_LED(constant_register_1_databus_3_led), .DataBus_4_LED(constant_register_1_databus_4_led),
    .DataBus_5_LED(constant_register_1_databus_5_led), .DataBus_6_LED(constant_register_1_databus_6_led),
    .DataBus_7_LED(constant_register_1_databus_7_led),
    .MEM_BUS_LOAD_LED(constant_register_1_mem_bus_load_led),
    .Register_3_LED(constant_register_1_register_3_led), .Register_4_LED(constant_register_1_register_4_led),
    .Register_5_LED(constant_register_1_register_5_led), .Register_6_LED(constant_register_1_register_6_led),
    .Register_7_LED(constant_register_1_register_7_led),
    .DATA_ASSERT_LED(constant_register_1_data_assert_led),
    .Regsiter_0_LED(constant_register_1_regsiter_0_led), .Register_1_LED(constant_register_1_register_1_led),
    .Register_2_LED(constant_register_1_register_2_led), .DATA_BUS_OUT(DATA_BUS));
  LedBar ledbar_14 (
    .led0(constant_register_1_databus_7_led), .led1(constant_register_1_databus_6_led),
    .led2(constant_register_1_databus_5_led), .led3(constant_register_1_databus_4_led),
    .led4(constant_register_1_databus_3_led), .led5(constant_register_1_databus_2_led),
    .led6(constant_register_1_databus_1_led), .led7(constant_register_1_databus_0_led));
  LED led_43 (.in(data_register_1_rhs_assert_led));
  LED led_44 (.in(data_register_1_load_led));
  LED led_45 (.in(data_register_2_rhs_assert_led));
  LED led_46 (.in(data_register_2_load_led));
  LED led_47 (.in(data_register_3_rhs_assert_led));
  LED led_48 (.in(data_register_3_load_led));
  LED led_49 (.in(data_register_4_rhs_assert_led));
  LED led_50 (.in(data_register_4_load_led));
  assign MEM_BUS = DATA_TO_MEM_ASSERT ? DATA_BUS : 8'bz;  // Controlled_Buffer controlled_buffer_2
  assign DATA_BUS = bus_control_1_mem_control[3] ? MEM_BUS : 8'bz;  // Controlled_Buffer controlled_buffer_3
  // LedBar #(.inputtype("row")) ledbar_15: pin names not known; wires that end beside it: MEM_BUS
  not not_3 (not_3_out, DATA_TO_MEM_ASSERT);
  assign MEM_BUS = not_3_out ? controlled_buffer_1_out : 8'bz;  // Controlled_Buffer controlled_buffer_4
  assign controlled_buffer_1_out = ADDR_BUS[15] ? ram_1_dout : 8'bz;  // Controlled_Buffer controlled_buffer_5
  // LedBar #(.inputtype("row")) ledbar_16: pin names not known; wires that end beside it: DATA_BUS
  Clock clock_2 ();  // open: out
  Button button_1 (.out(RST_BUTTON));
  ROM #(.addrWidth(4)) rom_2 (.addr(ALU_CONTROL), .data(rom_2_data));
  // LedBar #(.inputtype("row")) ledbar_17: pin names not known; wires that end beside it: ALU_LHS_BUS
  // LedBar #(.inputtype("row")) ledbar_18: pin names not known; wires that end beside it: ALU_RHS_BUS
  nor nor_3 (nor_3_out, ALU_CONTROL[0], ALU_CONTROL[1], ALU_CONTROL[2], ALU_CONTROL[3]);
  Register register_1 (.D(register_2_q), .en(1'b1), .clk(CLK), .Q(register_1_q), .clr(RST));
  Register register_2 (.D(controlled_buffer_6_out), .en(1'b1), .clk(CLK), .Q(register_2_q), .clr(RST));
  // LedBar #(.inputtype("row"), .matrixcols(5)) ledbar_19: pin names not known; wires that end beside it: ALU_FLAGS
  assign controlled_buffer_6_out = nor_4_out ? MEM_BUS : 8'bz;  // Controlled_Buffer controlled_buffer_6
  Pull_Resistor pull_resistor_1 (.node(controlled_buffer_6_out));
  nor nor_4 (nor_4_out, or_3_out, NO_FETCH);
  and and_1 (and_1_out, NO_FETCH, BUS_REQUEST);
  LED led_51 (.in(and_1_out));
  or or_2 (or_2_out, CLK, nor_3_out);
  Pull_Resistor pull_resistor_2 (.node(ALU_FLAGS[4]));
  Multiplexer #(.select(2)) multiplexer_1 (
    .in0(rom_2_data[0]), .in1(rom_2_data[1]), .in2(rom_2_data[2]), .in3(rom_2_data[3]),
    .out(multiplexer_10_out[3]));  // open: sel
  Multiplexer #(.select(2)) multiplexer_2 (
    .in0(rom_2_data[0]), .in1(rom_2_data[1]), .in2(rom_2_data[2]), .in3(rom_2_data[3]),
    .out(multiplexer_11_out[3]), .sel({ALU_RHS_BUS[7], ALU_LHS_BUS[7]}));
  Multiplexer multiplexer_3 (.in0(PC_RA_FLIP), .in1(1'b0), .out(multiplexer_3_out[13]), .sel(RST));
  Multiplexer #(.select(2)) multiplexer_4 (
    .in0(rom_2_data[0]), .in1(rom_2_data[1]), .in2(rom_2_data[2]), .in3(rom_2_data[3]),
    .out(multiplexer_10_out[2]));  // open: sel
  Multiplexer #(.select(2)) multiplexer_5 (
    .in0(rom_2_data[0]), .in1(rom_2_data[1]), .in2(rom_2_data[2]), .in3(rom_2_data[3]),
    .out(multiplexer_10_out[1]));  // open: sel
  Multiplexer #(.select(2)) multiplexer_6 (
    .in0(rom_2_data[0]), .in1(rom_2_data[1]), .in2(rom_2_data[2]), .in3(rom_2_data[3]),
    .out(multiplexer_11_out[2]), .sel({ALU_RHS_BUS[6], ALU_LHS_BUS[6]}));
  Multiplexer #(.select(2)) multiplexer_7 (
    .in0(rom_2_data[0]), .in1(rom_2_data[1]), .in2(rom_2_data[2]), .in3(rom_2_data[3]),
    .out(multiplexer_11_out[1]), .sel({ALU_RHS_BUS[5], ALU_LHS_BUS[5]}));
  ROM #(.addrWidth(14)) rom_3 (.addr({multiplexer_3_out[13], ALU_FLAGS, register_2_q}), .data(rom_3_data));
  ROM #(.addrWidth(14)) rom_4 (.addr({multiplexer_3_out[13], ALU_FLAGS, register_2_q}), .data(rom_4_data));
  ROM #(.addrWidth(14)) rom_5 (.addr({multiplexer_3_out[13], ALU_FLAGS, controlled_buffer_6_out}), .data(rom_5_data));
  ROM #(.addrWidth(14)) rom_6 (.addr({multiplexer_3_out[13], ALU_FLAGS, controlled_buffer_6_out}), .data(rom_6_data));
  or or_3 (or_3_out, BUS_REQUEST, RST);
  Multiplexer #(.select(2)) multiplexer_8 (
    .in0(ALU_FLAGS[4]), .in1(ALU_LHS_BUS[7]), .in2(ALU_LHS_BUS[0]), .in3(1'b0), .out(multiplexer_8_out),
    .sel(rom_2_data[5:4]));
  Multiplexer #(.select(2), .width(8)) multiplexer_9 (
    .in0(ALU_LHS_BUS), .in1({ALU_LHS_BUS[6:0], ALU_FLAGS[4]}), .in2({ALU_FLAGS[4], ALU_LHS_BUS[7:1]}),
    .in3({8{1'b0}}), .out(multiplexer_9_out), .sel(rom_2_data[5:4]));
  Multiplexer #(.select(2)) multiplexer_10 (
    .in0(rom_2_data[0]), .in1(rom_2_data[1]), .in2(rom_2_data[2]), .in3(rom_2_data[3]),
    .out(multiplexer_10_out[0]));  // open: sel
  Multiplexer #(.select(2)) multiplexer_11 (
    .in0(rom_2_data[0]), .in1(rom_2_data[1]), .in2(rom_2_data[2]), .in3(rom_2_data[3]),
    .out(multiplexer_11_out[0]), .sel({ALU_RHS_BUS[4], ALU_LHS_BUS[4]}));
  // LedBar #(.inputtype("row")) ledbar_20: pin names not known; wires that end beside it: register_1_q
  // LedBar #(.inputtype("row")) ledbar_21: pin names not known; wires that end beside it: register_2_q
  // LedBar #(.inputtype("row")) ledbar_22: pin names not known; wires that end beside it: controlled_buffer_6_out, ledbar_22_p2
  Register #(.width(2)) register_3 (.D(rom_2_data[7:6]), .en(1'b1), .clk(or_2_out), .Q(register_3_q), .clr(RST));
  Register #(.width(1)) register_4 (.D(multiplexer_8_out), .en(1'b1), .clk(or_2_out), .Q(ALU_FLAGS[4]), .clr(RST));
  Register register_5 (.D(multiplexer_9_out), .en(1'b1), .clk(or_2_out), .Q(register_5_q), .clr(RST));
  Register register_6 (
    .D({multiplexer_11_out, multiplexer_10_out}), .en(1'b1), .clk(or_2_out), .Q(register_6_q), .clr(RST));
  Register register_7 (
    .D(rom_3_data), .en(1'b1), .clk(CLK),
    .Q({BUS_REQUEST, ADDR_ASSERT_CONTROL, register_7_q[3], PC_RA_FLIP, INC_CONTROL}), .clr(1'b0));
  Register register_8 (
    .D(rom_4_data), .en(1'b1), .clk(CLK), .Q({DATA_BUS_LOAD_CONTROL, DATA_BUS_ASSERT_CONTROL}), .clr(1'b0));
  Register register_9 (
    .D(rom_5_data), .en(1'b1), .clk(CLK), .Q({NO_FETCH, XFER_ASSERT_CONTROL, DEC_XFER_LOAD_CONTROL}),
    .clr(1'b0));
  Register register_10 (
    .D(rom_6_data), .en(1'b1), .clk(CLK), .Q({ALU_CONTROL, LHS_BUS_ASSERT_CONTROL, RHS_BUS_ASSERT_CONTROL}),
    .clr(1'b0));
  Clock clock_3 (.out(ledbar_22_p2));
  // LedBar #(.inputtype("row")) ledbar_23: pin names not known; wires that end beside it: register_5_q, register_3_q
  // LedBar #(.inputtype("row")) ledbar_24: pin names not known; wires that end beside it: register_6_q
  // LedBar #(.inputtype("row")) ledbar_25: pin names not known; wires that end beside it: {ALU_CONTROL, LHS_BUS_ASSERT_CONTROL, RHS_BUS_ASSERT_CONTROL}
  Multiplexer #(.select(2)) multiplexer_12 (
    .in0(1'b0), .in1(register_11_q), .in2(1'b1), .in3(1'b0), .out(multiplexer_12_out));  // open: sel
  Adder adder_1 (
    .a(register_5_q), .b(register_6_q), .out({ALU_FLAGS[1], adder_1_out}), .cin(multiplexer_12_out),
    .cout(ALU_FLAGS[3]));
  Register #(.width(1)) register_11 (.D(ALU_FLAGS[3]), .en(1'b1), .clk(or_2_out), .Q(register_11_q), .clr(RST));
  // LedBar #(.inputtype("row")) ledbar_26: pin names not known; wires that end beside it: {DATA_BUS_LOAD_CONTROL, DATA_BUS_ASSERT_CONTROL}
  // LedBar #(.inputtype("row")) ledbar_27: pin names not known; wires that end beside it: {NO_FETCH, XFER_ASSERT_CONTROL, DEC_XFER_LOAD_CONTROL}
  assign controlled_buffer_7_out = not_4_out ? LCD_LOAD : 1'bz;  // Controlled_Buffer controlled_buffer_7
  not not_4 (not_4_out, buffer_1_out);
  buf buffer_1 (buffer_1_out, DATA_BUS[7]);
  Pull_Resistor pull_resistor_3 (.node(buffer_1_out));
  xor xor_1 (xor_1_out, register_5_q[7], ALU_FLAGS[1]);
  xor xor_2 (xor_2_out, ALU_FLAGS[1], register_6_q[7]);
  // LedBar #(.inputtype("row")) ledbar_28: pin names not known; wires that end beside it: {BUS_REQUEST, ADDR_ASSERT_CONTROL, register_7_q[3], PC_RA_FLIP, INC_CONTROL}
  TTY tty_1 (.data(DATA_BUS[6:0]), .clk(controlled_buffer_7_out), .we(1'b1), .clr(controlled_buffer_8_out));
  Pull_Resistor pull_resistor_4 (.node(controlled_buffer_7_out));
  assign controlled_buffer_8_out = LCD_LOAD ? buffer_1_out : 1'bz;  // Controlled_Buffer controlled_buffer_8
  Pull_Resistor pull_resistor_5 (.node(controlled_buffer_8_out));
  nor nor_5 (ALU_FLAGS[2], adder_1_out[0], adder_1_out[1], adder_1_out[2], adder_1_out[3], adder_1_out[4], adder_1_out[5], adder_1_out[6], ALU_FLAGS[1]);
  and and_2 (ALU_FLAGS[0], xor_1_out, xor_2_out);
  LED led_52 (.in(ALU_FLAGS[4]));
  LED led_53 (.in(ALU_FLAGS[3]));
  LED led_54 (.in(ALU_FLAGS[2]));
  LED led_55 (.in(ALU_FLAGS[1]));
  LED led_56 (.in(ALU_FLAGS[0]));
  assign DATA_BUS = ALU_ASSERT ? {ALU_FLAGS[1], adder_1_out} : 8'bz;  // Controlled_Buffer controlled_buffer_9
  // LedBar #(.inputtype("row")) ledbar_29: pin names not known; wires that end beside it: {ALU_FLAGS[1], adder_1_out}

  // Notes on the sheet:
  //   Address Registers
  //   contents of rom_1 (hex, n*v repeats v):
  //   5 6a 6 0 58 0 5 e4 6 0 27 5 74 6 0 58 0 5 6f 6 0 58 0 58 0 1 1 e1 e6 eb 72 0 5 f7 6 0 27 5 74 6 0 58
  //   0 2a 1b 5 a6 6 0 58 0 36 1 3d 37 78 0 5 cb 6 0 58 0 72 0 5 6f 6 0 58 0 78 13 18 89 99 1d 22 5 1e 6 0
  //   5f 68 5 58 6 0 5f 60 30 31 32 33 34 35 36 37 38 39 41 42 43 44 45 46 1 80 37 59 0 1 a 37 59 0 2a 76
  //   77 0 5 81 6 0 29 5 89 6 0 40 35 fc 5f 65 37 5f 71 7d 7c 29 59 0 72 73 74 75 3 5a 4 0 2 f c4 e1 89 99
  //   13 18 7b 7a 79 48 37 78 59 0 72 73 74 75 72 0 3 5a 4 0 2 f 4*84 c4 8e bf 15 1a 48 37 78 c4 8e bf 15
  //   1a 48 37 7b 7a 79 78 59 0 24 76 77 72 0 5 a6 6 0 7 58 0 78 0 5 a6 6 0 58 0 7d 7c 23 59 0 46 69 62 6f
  //   6e 61 63 63 69 20 53 65 71 75 65 6e 63 65 0 56 61 6c 75 65 20
  //   Clock and Reset
  //   Program Counter
  //   Return Address
  //   Stack Pointer
  //   Source Index
  //   Destination Index
  //   Transfer Register
  //   Bus Control
  //   Memory
  //   A Register
  //   B Register
  //   C Register
  //   D Register
  //   Constant Register
  //   Data Bus
  //   Data Registers
  //   contents of rom_2 (hex, n*v repeats v):
  //   0 10 20 c 4c 80 40 83 43 f 38 3e 36 33 30
  //   contents of rom_3 (hex, n*v repeats v):
  //   52*10 11 12 13 9*10 4*c0 4*d0 4*e0 4*c0 4*d0 4*e0 24 24 5*10 90 18*10 6*b0 6*b1 182*10 11 12 13 9*10
  //   4*c0 4*d0 4*e0 4*c0 4*d0 4*e0 24 24 5*10 90 18*10 6*b0 6*b1 182*10 11 12 13 9*10 4*c0 4*d0 4*e0 4*c0
  //   4*d0 4*e0 24 24 5*10 90 18*10 6*b0 6*b1 182*10 11 12 13 9*10 4*c0 4*d0 4*e0 4*c0 4*d0 4*e0 24 24
  //   5*10 90 18*10 6*b0 6*b1 182*10 11 12 13 9*10 4*c0 4*d0 4*e0 4*c0 4*d0 4*e0 24 24 5*10 90 18*10 6*b0
  //   6*b1 182*10 11 12 13 9*10 4*c0 4*d0 4*e0 4*c0 4*d0 4*e0 24 24 5*10 90 18*10 6*b0 6*b1 182*10 11 12
  //   13 9*10 4*c0 4*d0 4*e0 4*c0 4*d0 4*e0 24 24 5*10 90 18*10 6*b0 6*b1 182*10 11 12 13 9*10 4*c0 4*d0
  //   4*e0 4*c0 4*d0 4*e0 24 24 5*10 90 18*10 6*b0 6*b1 182*10 11 12 13 9*10 4*c0 4*d0 4*e0 4*c0 4*d0 4*e0
  //   24 24 5*10 90 18*10 6*b0 6*b1 182*10 11 12 13 9*10 4*c0 4*d0 4*e0 4*c0 4*d0 4*e0 24 24 5*10 90 18*10
  //   6*b0 6*b1 182*10 11 12 13 9*10 4*c0 4*d0 4*e0 4*c0 4*d0 4*e0 24 24 5*10 90 18*10 6*b0 6*b1 182*10 11
  //   12 13 9*10 4*c0 4*d0 4*e0 4*c0 4*d0 4*e0 24 24 5*10 90 18*10 6*b0 6*b1 182*10 11 12 13 9*10 4*c0
  //   4*d0 4*e0 4*c0 4*d0 4*e0 24 24 5*10 90 18*10 6*b0 6*b1 182*10 11 12 13 9*10 4*c0 4*d0 4*e0 4*c0 4*d0
  //   4*e0 24 24 5*10 90 18*10 6*b0 6*b1 182*10 11 12 13 9*10 4*c0 4*d0 4*e0 4*c0 4*d0 4*e0 24 24 5*10 90
  //   18*10 6*b0 6*b1 182*10 11 12 13 9*10 4*c0 4*d0 4*e0 4*c0 4*d0 4*e0 24 24 5*10 90 18*10 6*b0 6*b1
  //   182*10 11 12 13 9*10 4*c0 4*d0 4*e0 4*c0 4*d0 4*e0 24 24 5*10 90 18*10 6*b0 6*b1 182*10 11 12 13
  //   9*10 4*c0 4*d0 4*e0 4*c0 4*d0 4*e0 24 24 5*10 90 18*10 6*b0 6*b1 182*10 11 12 13 9*10 4*c0 4*d0 4*e0
  //   4*c0 4*d0 4*e0 24 24 5*10 90 18*10 6*b0 6*b1 182*10 11 12 13 9*10 4*c0 4*d0 4*e0 4*c0 4*d0 4*e0 24
  //   24 5*10 90 18*10 6*b0 6*b1 182*10 11 12 13 9*10 4*c0 4*d0 4*e0 4*c0 4*d0 4*e0 24 24 5*10 90 18*10
  //   6*b0 6*b1 182*10 11 12 13 9*10 4*c0 4*d0 4*e0 4*c0 4*d0 4*e0 24 24 5*10 90 18*10 6*b0 6*b1 182*10 11
  //   12 13 9*10 4*c0 4*d0 4*e0 4*c0 4*d0 4*e0 24 24 5*10 90 18*10 6*b0 6*b1 182*10 11 12 13 9*10 4*c0
  //   4*d0 4*e0 4*c0 4*d0 4*e0 24 24 5*10 90 18*10 6*b0 6*b1 182*10 11 12 13 9*10 4*c0 4*d0 4*e0 4*c0 4*d0
  //   4*e0 24 24 5*10 90 18*10 6*b0 6*b1 182*10 11 12 13 9*10 4*c0 4*d0 4*e0 4*c0 4*d0 4*e0 24 24 5*10 90
  //   18*10 6*b0 6*b1 182*10 11 12 13 9*10 4*c0 4*d0 4*e0 4*c0 4*d0 4*e0 24 24 5*10 90 18*10 6*b0 6*b1
  //   182*10 11 12 13 9*10 4*c0 4*d0 4*e0 4*c0 4*d0 4*e0 24 24 5*10 90 18*10 6*b0 6*b1 182*10 11 12 13
  //   9*10 4*c0 4*d0 4*e0 4*c0 4*d0 4*e0 24 24 5*10 90 18*10 6*b0 6*b1 182*10 11 12 13 9*10 4*c0 4*d0 4*e0
  //   4*c0 4*d0 4*e0 24 24 5*10 90 18*10 6*b0 6*b1 182*10 11 12 13 9*10 4*c0 4*d0 4*e0 4*c0 4*d0 4*e0 24
  //   24 5*10 90 18*10 6*b0 6*b1 182*10 11 12 13 9*10 4*c0 4*d0 4*e0 4*c0 4*d0 4*e0 24 24 5*10 90 18*10
  //   6*b0 6*b1 130*10 52*24 25 26 27 9*24 4*c4 4*d4 4*e4 4*c4 4*d4 4*e4 10 10 5*24 a4 18*24 6*b4 6*b5
  //   182*24 25 26 27 9*24 4*c4 4*d4 4*e4 4*c4 4*d4 4*e4 10 10 5*24 a4 18*24 6*b4 6*b5 182*24 25 26 27
  //   9*24 4*c4 4*d4 4*e4 4*c4 4*d4 4*e4 10 10 5*24 a4 18*24 6*b4 6*b5 182*24 25 26 27 9*24 4*c4 4*d4 4*e4
  //   4*c4 4*d4 4*e4 10 10 5*24 a4 18*24 6*b4 6*b5 182*24 25 26 27 9*24 4*c4 4*d4 4*e4 4*c4 4*d4 4*e4 10
  //   10 5*24 a4 18*24 6*b4 6*b5 182*24 25 26 27 9*24 4*c4 4*d4 4*e4 4*c4 4*d4 4*e4 10 10 5*24 a4 18*24
  //   6*b4 6*b5 182*24 25 26 27 9*24 4*c4 4*d4 4*e4 4*c4 4*d4 4*e4 10 10 5*24 a4 18*24 6*b4 6*b5 182*24 25
  //   26 27 9*24 4*c4 4*d4 4*e4 4*c4 4*d4 4*e4 10 10 5*24 a4 18*24 6*b4 6*b5 182*24 25 26 27 9*24 4*c4
  //   4*d4 4*e4 4*c4 4*d4 4*e4 10 10 5*24 a4 18*24 6*b4 6*b5 182*24 25 26 27 9*24 4*c4 4*d4 4*e4 4*c4 4*d4
  //   4*e4 10 10 5*24 a4 18*24 6*b4 6*b5 182*24 25 26 27 9*24 4*c4 4*d4 4*e4 4*c4 4*d4 4*e4 10 10 5*24 a4
  //   18*24 6*b4 6*b5 182*24 25 26 27 9*24 4*c4 4*d4 4*e4 4*c4 4*d4 4*e4 10 10 5*24 a4 18*24 6*b4 6*b5
  //   182*24 25 26 27 9*24 4*c4 4*d4 4*e4 4*c4 4*d4 4*e4 10 10 5*24 a4 18*24 6*b4 6*b5 182*24 25 26 27
  //   9*24 4*c4 4*d4 4*e4 4*c4 4*d4 4*e4 10 10 5*24 a4 18*24 6*b4 6*b5 182*24 25 26 27 9*24 4*c4 4*d4 4*e4
  //   4*c4 4*d4 4*e4 10 10 5*24 a4 18*24 6*b4 6*b5 182*24 25 26 27 9*24 4*c4 4*d4 4*e4 4*c4 4*d4 4*e4 10
  //   10 5*24 a4 18*24 6*b4 6*b5 182*24 25 26 27 9*24 4*c4 4*d4 4*e4 4*c4 4*d4 4*e4 10 10 5*24 a4 18*24
  //   6*b4 6*b5 182*24 25 26 27 9*24 4*c4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
  //   contents of rom_4 (hex, n*v repeats v):
  //   0 15 25 35 45 65 75 12 13 14 21 23 24 31 32 34 41 42 43 61 62 63 64 71 72 73 74 16 26 36 46 17 27 37
  //   47 20*0 e1 8*0 1f 2f 3f 4f 1f 2f 3f 4f 1f 2f 3f 4f f1 f2 f3 f4 f1 f2 f3 f4 f1 f2 f3 f4 26*0 f1 f2 f3
  //   f4 f6 f7 1f 2f 3f 4f 6f 7f 0 0 18 28 38 48 18 28 38 48 18 18 18 28 28 28 38 38 38 48 48 48 18 18 18
  //   28 28 28 38 38 38 48 48 48 18 18 18 28 28 28 38 38 38 48 48 48 18 18 18 28 28 28 38 38 38 48 48 48
  //   18 28 38 48 18 28 38 48 18 28 38 48 18 18 18 28 28 28 38 38 38 48 48 48 18 18 18 28 28 28 38 38 38
  //   48 48 48 4*18 4*28 4*38 4*48 18 28 38 48 17*0 15 25 35 45 65 75 12 13 14 21 23 24 31 32 34 41 42 43
  //   61 62 63 64 71 72 73 74 16 26 36 46 17 27 37 47 20*0 e1 8*0 1f 2f 3f 4f 1f 2f 3f 4f 1f 2f 3f 4f f1
  //   f2 f3 f4 f1 f2 f3 f4 f1 f2 f3 f4 26*0 f1 f2 f3 f4 f6 f7 1f 2f 3f 4f 6f 7f 0 0 18 28 38 48 18 28 38
  //   48 18 18 18 28 28 28 38 38 38 48 48 48 18 18 18 28 28 28 38 38 38 48 48 48 18 18 18 28 28 28 38 38
  //   38 48 48 48 18 18 18 28 28 28 38 38 38 48 48 48 18 28 38 48 18 28 38 48 18 28 38 48 18 18 18 28 28
  //   28 38 38 38 48 48 48 18 18 18 28 28 28 38 38 38 48 48 48 4*18 4*28 4*38 4*48 18 28 38 48 17*0 15 25
  //   35 45 65 75 12 13 14 21 23 24 31 32 34 41 42 43 61 62 63 64 71 72 73 74 16 26 36 46 17 27 37 47 20*0
  //   e1 8*0 1f 2f 3f 4f 1f 2f 3f 4f 1f 2f 3f 4f f1 f2 f3 f4 f1 f2 f3 f4 f1 f2 f3 f4 26*0 f1 f2 f3 f4 f6
  //   f7 1f 2f 3f 4f 6f 7f 0 0 18 28 38 48 18 28 38 48 18 18 18 28 28 28 38 38 38 48 48 48 18 18 18 28 28
  //   28 38 38 38 48 48 48 18 18 18 28 28 28 38 38 38 48 48 48 18 18 18 28 28 28 38 38 38 48 48 48 18 28
  //   38 48 18 28 38 48 18 28 38 48 18 18 18 28 28 28 38 38 38 48 48 48 18 18 18 28 28 28 38 38 38 48 48
  //   48 4*18 4*28 4*38 4*48 18 28 38 48 17*0 15 25 35 45 65 75 12 13 14 21 23 24 31 32 34 41 42 43 61 62
  //   63 64 71 72 73 74 16 26 36 46 17 27 37 47 20*0 e1 8*0 1f 2f 3f 4f 1f 2f 3f 4f 1f 2f 3f 4f f1 f2 f3
  //   f4 f1 f2 f3 f4 f1 f2 f3 f4 26*0 f1 f2 f3 f4 f6 f7 1f 2f 3f 4f 6f 7f 0 0 18 28 38 48 18 28 38 48 18
  //   18 18 28 28 28 38 38 38 48 48 48 18 18 18 28 28 28 38 38 38 48 48 48 18 18 18 28 28 28 38 38 38 48
  //   48 48 18 18 18 28 28 28 38 38 38 48 48 48 18 28 38 48 18 28 38 48 18 28 38 48 18 18 18 28 28 28 38
  //   38 38 48 48 48 18 18 18 28 28 28 38 38 38 48 48 48 4*18 4*28 4*38 4*48 18 28 38 48 17*0 15 25 35 45
  //   65 75 12 13 14 21 23 24 31 32 34 41 42 43 61 62 63 64 71 72 73 74 16 26 36 46 17 27 37 47 20*0 e1
  //   8*0 1f 2f 3f 4f 1f 2f 3f 4f 1f 2f 3f 4f f1 f2 f3 f4 f1 f2 f3 f4 f1 f2 f3 f4 26*0 f1 f2 f3 f4 f6 f7
  //   1f 2f 3f 4f 6f 7f 0 0 18 28 38 48 18 28 38 48 18 18 18 28 28 28 38 38 38 48 48 48 18 18 18 28 28 28
  //   38 38 38 48 48 48 18 18 18 28 28 28 38 38 38 48 48 48 18 18 18 28 28 28 38 38 38 48 48 48 18 28 38
  //   48 18 28 38 48 18 28 38 48 18 18 18 28 28 28 38 38 38 48 48 48 18 18 18 28 28 28 38 38 38 48 48 48
  //   4*18 4*28 4*38 4*48 18 28 38 48 17*0 15 25 35 45 65 75 12 13 14 21 23 24 31 32 34 41 42 43 61 62 63
  //   64 71 72 73 74 16 26 36 46 17 27 37 47 20*0 e1 8*0 1f 2f 3f 4f 1f 2f 3f 4f 1f 2f 3f 4f f1 f2 f3 f4
  //   f1 f2 f3 f4 f1 f2 f3 f4 26*0 f1 f2 f3 f4 f6 f7 1f 2f 3f 4f 6f 7f 0 0 18 28 38 48 18 28 38 48 18 18
  //   18 28 28 28 38 38 38 48 48 48 18 18 18 28 28 28 38 38 38 48 48 48 18 18 18 28 28 28 38 38 38 48 48
  //   48 18 18 18 28 28 28 38 38 38 48 48 48 18 28 38 48 18 28 38 48 18 28 38 48 18 18 18 28 28 28 38 38
  //   38 48 48 48 18 18 18 28 28 28 38 38 38 48 48 48 4*18 4*28 4*38 4*48 18 28 38 48 17*0 15 25 35 45 65
  //   75 12 13 14 21 23 24 31 32 34 41 42 43 61 62 63 64 71 72 73 74 16 26 36 46 17 27 37 47 20*0 e1 8*0
  //   1f 2f 3f 4f 1f 2f 3f 4f 1f 2f 3f 4f f1 f2 f3 f4 f1 f2 f3 f4 f1 f2 f3 f4 26*0 f1 f2 f3 f4 f6 f7 1f 2f
  //   3f 4f 6f 7f 0 0 18 28 38 48 18 28 38 48 18 18 18 28 28 28 38 38 38 48 48 48 18 18 18 28 28 28 38 38
  //   38 48 48 48 18 18 18 28 28 28 38 38 38 48 48 48 18 18 18 28 28 28 38 38 38 48 48 48 18 28 38 48 18
  //   28 38 48 18 28 38 48 18 18 18 28 28 28 38 38 38 48 48 48 18 18 18 28 28 28 38 38 38 48 48 48 4*18
  //   4*28 4*38 4*48 18 28 38 48 17*0 15 25 35 45 65 75 12 13 14 21 23 24 31 32 34 41 42 43 61 62 63 64 71
  //   72 73 74 16 26 36 46 17 27 37 47 20*0 e1 8*0 1f 2f 3f 4f 1f 2f 3f 4f 1f 2f 3f 4f f1 f2 f3 f4 f1 f2
  //   f3 f4 f1 f2 f3 f4 26*0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
  //   contents of rom_5 (hex, n*v repeats v):
  //   0 6*88 28*0 62 26 63 36 64 46 65 56 45 54 4*0 b c d 36*0 62 7*0 61 0 61 0 61 0 61 0 61 0 61 0 61 0
  //   61 0 61 51 6*b 137*0 6*88 28*0 62 26 63 36 64 46 65 56 45 54 4*0 b c d 36*0 62 7*0 61 61 0 0 61 0 61
  //   0 61 0 61 61 0 61 61 0 61 51 6*b 137*0 6*88 28*0 62 26 63 36 64 46 65 56 45 54 4*0 b c d 36*0 62 7*0
  //   61 0 61 61 0 0 61 0 61 0 61 61 0 61 0 0 61 51 6*b 137*0 6*88 28*0 62 26 63 36 64 46 65 56 45 54 4*0
  //   b c d 36*0 62 7*0 61 61 0 61 0 0 61 0 61 0 61 0 61 0 0 0 61 51 6*b 137*0 6*88 28*0 62 26 63 36 64 46
  //   65 56 45 54 4*0 b c d 36*0 62 7*0 61 0 61 0 61 61 0 0 61 61 0 0 61 0 0 0 61 51 6*b 137*0 6*88 28*0
  //   62 26 63 36 64 46 65 56 45 54 4*0 b c d 36*0 62 7*0 61 61 0 0 61 61 0 0 61 61 0 61 4*0 61 51 6*b
  //   137*0 6*88 28*0 62 26 63 36 64 46 65 56 45 54 4*0 b c d 36*0 62 7*0 61 0 61 61 0 61 0 0 61 61 0 61 0
  //   61 0 0 61 51 6*b 137*0 6*88 28*0 62 26 63 36 64 46 65 56 45 54 4*0 b c d 36*0 62 7*0 61 61 0 61 0 61
  //   0 0 61 61 0 0 61 61 0 0 61 51 6*b 137*0 6*88 28*0 62 26 63 36 64 46 65 56 45 54 4*0 b c d 36*0 62
  //   7*0 61 0 61 0 61 0 61 61 0 61 0 0 61 0 61 0 61 51 6*b 137*0 6*88 28*0 62 26 63 36 64 46 65 56 45 54
  //   4*0 b c d 36*0 62 7*0 61 61 0 0 61 0 61 61 0 61 0 61 0 61 61 0 61 51 6*b 137*0 6*88 28*0 62 26 63 36
  //   64 46 65 56 45 54 4*0 b c d 36*0 62 7*0 61 0 61 61 0 0 61 61 0 61 0 61 0 61 0 0 61 51 6*b 137*0 6*88
  //   28*0 62 26 63 36 64 46 65 56 45 54 4*0 b c d 36*0 62 7*0 61 61 0 61 0 0 61 61 0 61 0 0 61 0 0 0 61
  //   51 6*b 137*0 6*88 28*0 62 26 63 36 64 46 65 56 45 54 4*0 b c d 36*0 62 7*0 61 0 61 0 61 61 0 61 0 61
  //   0 0 61 0 0 0 61 51 6*b 137*0 6*88 28*0 62 26 63 36 64 46 65 56 45 54 4*0 b c d 36*0 62 7*0 61 61 0 0
  //   61 61 0 61 0 61 0 61 4*0 61 51 6*b 137*0 6*88 28*0 62 26 63 36 64 46 65 56 45 54 4*0 b c d 36*0 62
  //   7*0 61 0 61 61 0 61 0 61 0 61 0 61 0 61 0 0 61 51 6*b 137*0 6*88 28*0 62 26 63 36 64 46 65 56 45 54
  //   4*0 b c d 36*0 62 7*0 61 61 0 61 0 61 0 61 0 61 0 0 61 61 0 0 61 51 6*b 137*0 6*88 28*0 62 26 63 36
  //   64 46 65 56 45 54 4*0 b c d 36*0 62 7*0 61 0 61 0 61 0 61 0 61 0 61 0 61 0 61 61 0 51 6*b 137*0 6*88
  //   28*0 62 26 63 36 64 46 65 56 45 54 4*0 b c d 36*0 62 7*0 61 61 0 0 61 0 61 0 61 0 61 61 0 61 61 61 0
  //   51 6*b 137*0 6*88 28*0 62 26 63 36 64 46 65 56 45 54 4*0 b c d 36*0 62 7*0 61 0 61 61 0 0 61 0 61 0
  //   61 61 0 61 0 61 0 51 6*b 137*0 6*88 28*0 62 26 63 36 64 46 65 56 45 54 4*0 b c d 36*0 62 7*0 61 61 0
  //   61 0 0 61 0 61 0 61 0 61 0 0 61 0 51 6*b 137*0 6*88 28*0 62 26 63 36 64 46 65 56 45 54 4*0 b c d
  //   36*0 62 7*0 61 0 61 0 61 61 0 0 61 61 0 0 61 0 0 61 0 51 6*b 137*0 6*88 28*0 62 26 63 36 64 46 65 56
  //   45 54 4*0 b c d 36*0 62 7*0 61 61 0 0 61 61 0 0 61 61 0 61 0 0 0 61 0 51 6*b 137*0 6*88 28*0 62 26
  //   63 36 64 46 65 56 45 54 4*0 b c d 36*0 62 7*0 61 0 61 61 0 61 0 0 61 61 0 61 0 61 0 61 0 51 6*b
  //   137*0 6*88 28*0 62 26 63 36 64 46 65 56 45 54 4*0 b c d 36*0 62 7*0 61 61 0 61 0 61 0 0 61 61 0 0 61
  //   61 0 61 0 51 6*b 137*0 6*88 28*0 62 26 63 36 64 46 65 56 45 54 4*0 b c d 36*0 62 7*0 61 0 61 0 61 0
  //   61 61 0 61 0 0 61 0 61 61 0 51 6*b 137*0 6*88 28*0 62 26 63 36 64 46 65 56 45 54 4*0 b c d 36*0 62
  //   7*0 61 61 0 0 61 0 61 61 0 61 0 61 0 61 61 61 0 51 6*b 137*0 6*88 28*0 62 26 63 36 64 46 65 56 45 54
  //   4*0 b c d 36*0 62 7*0 61 0 61 61 0 0 61 61 0 61 0 61 0 61 0 61 0 51 6*b 137*0 6*88 28*0 62 26 63 36
  //   64 46 65 56 45 54 4*0 b c d 36*0 62 7*0 61 61 0 61 0 0 61 61 0 61 0 0 61 0 0 61 0 51 6*b 137*0 6*88
  //   28*0 62 26 63 36 64 46 65 56 45 54 4*0 b c d 36*0 62 7*0 61 0 61 0 61 61 0 61 0 61 0 0 61 0 0 61 0
  //   51 6*b 137*0 6*88 28*0 62 26 63 36 64 46 65 56 45 54 4*0 b c d 36*0 62 7*0 61 61 0 0 61 61 0 61 0 61
  //   0 61 0 0 0 61 0 51 6*b 137*0 6*88 28*0 62 26 63 36 64 46 65 56 45 54 4*0 b c d 36*0 62 7*0 61 0 61
  //   61 0 61 0 61 0 61 0 61 0 61 0 61 0 51 6*b 137*0 6*88 28*0 62 26 63 36 64 46 65 56 45 54 4*0 b c d
  //   36*0 62 7*0 61 61 0 61 0 61 0 61 0 61 0 0 61 61 0 61 0 51 6*b 137*0 6*88 28*0 61 16 63 36 64 46 65
  //   56 45 54 4*0 b c d 36*0 61 7*0 62 0 62 0 62 0 62 0 62 0 62 0 62 0 62 0 62 52 6*b 137*0 6*88 28*0 61
  //   16 63 36 64 46 65 56 45 54 4*0 b c d 36*0 61 7*0 62 62 0 0 62 0 62 0 62 0 62 62 0 62 62 0 62 52 6*b
  //   137*0 6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
  //   contents of rom_6 (hex, n*v repeats v):
  //   127*0 e0 10 14 18 1c 20 24 28 2c 31 32 33 34 36 37 38 39 3b 3c 3d 3e 41 42 43 44 46 47 48 49 4b 4c
  //   4d 4e 71 72 73 74 76 77 78 79 7b 7c 7d 7e 81 82 83 84 86 87 88 89 8b 8c 8d 8e 50 54 58 5c 60 64 68
  //   6c 90 94 98 9c a1 a2 a3 a4 a6 a7 a8 a9 ab ac ad ae b1 b2 b3 b4 b6 b7 b8 b9 bb bc bd be c0 c1 c2 c3
  //   c4 c5 c6 c7 c8 c9 ca cb cc cd ce cf d0 d1 d2 d3 71 72 73 74 76 77 78 79 7b 7c 7d 7e a0 a5 aa af
  //   127*0 e0 10 14 18 1c 20 24 28 2c 31 32 33 34 36 37 38 39 3b 3c 3d 3e 41 42 43 44 46 47 48 49 4b 4c
  //   4d 4e 71 72 73 74 76 77 78 79 7b 7c 7d 7e 81 82 83 84 86 87 88 89 8b 8c 8d 8e 50 54 58 5c 60 64 68
  //   6c 90 94 98 9c a1 a2 a3 a4 a6 a7 a8 a9 ab ac ad ae b1 b2 b3 b4 b6 b7 b8 b9 bb bc bd be c0 c1 c2 c3
  //   c4 c5 c6 c7 c8 c9 ca cb cc cd ce cf d0 d1 d2 d3 71 72 73 74 76 77 78 79 7b 7c 7d 7e a0 a5 aa af
  //   127*0 e0 10 14 18 1c 20 24 28 2c 31 32 33 34 36 37 38 39 3b 3c 3d 3e 41 42 43 44 46 47 48 49 4b 4c
  //   4d 4e 71 72 73 74 76 77 78 79 7b 7c 7d 7e 81 82 83 84 86 87 88 89 8b 8c 8d 8e 50 54 58 5c 60 64 68
  //   6c 90 94 98 9c a1 a2 a3 a4 a6 a7 a8 a9 ab ac ad ae b1 b2 b3 b4 b6 b7 b8 b9 bb bc bd be c0 c1 c2 c3
  //   c4 c5 c6 c7 c8 c9 ca cb cc cd ce cf d0 d1 d2 d3 71 72 73 74 76 77 78 79 7b 7c 7d 7e a0 a5 aa af
  //   127*0 e0 10 14 18 1c 20 24 28 2c 31 32 33 34 36 37 38 39 3b 3c 3d 3e 41 42 43 44 46 47 48 49 4b 4c
  //   4d 4e 71 72 73 74 76 77 78 79 7b 7c 7d 7e 81 82 83 84 86 87 88 89 8b 8c 8d 8e 50 54 58 5c 60 64 68
  //   6c 90 94 98 9c a1 a2 a3 a4 a6 a7 a8 a9 ab ac ad ae b1 b2 b3 b4 b6 b7 b8 b9 bb bc bd be c0 c1 c2 c3
  //   c4 c5 c6 c7 c8 c9 ca cb cc cd ce cf d0 d1 d2 d3 71 72 73 74 76 77 78 79 7b 7c 7d 7e a0 a5 aa af
  //   127*0 e0 10 14 18 1c 20 24 28 2c 31 32 33 34 36 37 38 39 3b 3c 3d 3e 41 42 43 44 46 47 48 49 4b 4c
  //   4d 4e 71 72 73 74 76 77 78 79 7b 7c 7d 7e 81 82 83 84 86 87 88 89 8b 8c 8d 8e 50 54 58 5c 60 64 68
  //   6c 90 94 98 9c a1 a2 a3 a4 a6 a7 a8 a9 ab ac ad ae b1 b2 b3 b4 b6 b7 b8 b9 bb bc bd be c0 c1 c2 c3
  //   c4 c5 c6 c7 c8 c9 ca cb cc cd ce cf d0 d1 d2 d3 71 72 73 74 76 77 78 79 7b 7c 7d 7e a0 a5 aa af
  //   127*0 e0 10 14 18 1c 20 24 28 2c 31 32 33 34 36 37 38 39 3b 3c 3d 3e 41 42 43 44 46 47 48 49 4b 4c
  //   4d 4e 71 72 73 74 76 77 78 79 7b 7c 7d 7e 81 82 83 84 86 87 88 89 8b 8c 8d 8e 50 54 58 5c 60 64 68
  //   6c 90 94 98 9c a1 a2 a3 a4 a6 a7 a8 a9 ab ac ad ae b1 b2 b3 b4 b6 b7 b8 b9 bb bc bd be c0 c1 c2 c3
  //   c4 c5 c6 c7 c8 c9 ca cb cc cd ce cf d0 d1 d2 d3 71 72 73 74 76 77 78 79 7b 7c 7d 7e a0 a5 aa af
  //   127*0 e0 10 14 18 1c 20 24 28 2c 31 32 33 34 36 37 38 39 3b 3c 3d 3e 41 42 43 44 46 47 48 49 4b 4c
  //   4d 4e 71 72 73 74 76 77 78 79 7b 7c 7d 7e 81 82 83 84 86 87 88 89 8b 8c 8d 8e 50 54 58 5c 60 64 68
  //   6c 90 94 98 9c a1 a2 a3 a4 a6 a7 a8 a9 ab ac ad ae b1 b2 b3 b4 b6 b7 b8 b9 bb bc bd be c0 c1 c2 c3
  //   c4 c5 c6 c7 c8 c9 ca cb cc cd ce cf d0 d1 d2 d3 71 72 73 74 76 77 78 79 7b 7c 7d 7e a0 a5 aa af
  //   127*0 e0 10 14 18 1c 20 24 28 2c 31 32 33 34 36 37 38 39 3b 3c 3d 3e 41 42 43 44 46 47 48 49 4b 4c
  //   4d 4e 71 72 73 74 76 77 78 79 7b 7c 7d 7e 81 82 83 84 86 87 88 89 8b 8c 8d 8e 50 54 58 5c 60 64 68
  //   6c 90 94 98 9c a1 a2 a3 a4 a6 a7 a8 a9 ab ac ad ae b1 b2 b3 b4 b6 b7 b8 b9 bb bc bd be c0 c1 c2 c3
  //   c4 c5 c6 c7 c8 c9 ca cb cc cd ce cf d0 d1 d2 d3 71 72 73 74 76 77 78 79 7b 7c 7d 7e a0 a5 aa af
  //   127*0 e0 10 14 18 1c 20 24 28 2c 31 32 33 34 36 37 38 39 3b 3c 3d 3e 41 42 43 44 46 47 48 49 4b 4c
  //   4d 4e 71 72 73 74 76 77 78 79 7b 7c 7d 7e 81 82 83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
  //   Control ROM Pipeline
  //   ALU
  //   Text Display
  //   LC
  //   C
  //   Z
  //   S
  //   O
endmodule

module Data_Register (
  input  DATA_ASSERT,
  input  LOAD,
  input  RST_IN,
  input  LHS_ASSERT,
  input  RHS_ASSERT,
  input  [7:0] DATA_BUS_IN,
  output Regsiter_0_LED,
  output Register_1_LED,
  output Register_2_LED,
  output Register_3_LED,
  output Register_4_LED,
  output Register_5_LED,
  output Register_6_LED,
  output Register_7_LED,
  output [7:0] DATA_BUS_OUT,
  output DATA_ASSERT_LED,
  output LOAD_LED,
  output [7:0] LHS_BUS_OUT,
  output LHS_ASSERT_LED,
  output [7:0] RHS_BUS_OUT,
  output RHS_ASSERT_LED
);

  Register register_1 (
    .D(DATA_BUS_IN), .en(1'b1), .clk(LOAD),
    .Q({Register_7_LED, Register_6_LED, Register_5_LED, Register_4_LED, Register_3_LED, Register_2_LED, Register_1_LED, Regsiter_0_LED}),
    .clr(RST_IN));
  assign DATA_BUS_OUT = DATA_ASSERT ? {Register_7_LED, Register_6_LED, Register_5_LED, Register_4_LED, Register_3_LED, Register_2_LED, Register_1_LED, Regsiter_0_LED} : 8'bz;  // Controlled_Buffer controlled_buffer_1
  assign LHS_BUS_OUT = LHS_ASSERT ? {Register_7_LED, Register_6_LED, Register_5_LED, Register_4_LED, Register_3_LED, Register_2_LED, Register_1_LED, Regsiter_0_LED} : 8'bz;  // Controlled_Buffer controlled_buffer_2
  assign RHS_BUS_OUT = RHS_ASSERT ? {Register_7_LED, Register_6_LED, Register_5_LED, Register_4_LED, Register_3_LED, Register_2_LED, Register_1_LED, Regsiter_0_LED} : 8'bz;  // Controlled_Buffer controlled_buffer_3

  assign DATA_ASSERT_LED = DATA_ASSERT;
  assign LHS_ASSERT_LED = LHS_ASSERT;
  assign LOAD_LED = LOAD;
  assign RHS_ASSERT_LED = RHS_ASSERT;
endmodule

module Address_Register (
  input  RST_IN,
  input  [15:0] XFER_BUS_IN,
  input  LOAD,
  input  XFER_ASSERT,
  input  INC,
  input  DEC,
  input  CLK_IN,
  input  ADDR_ASSERT,
  output Counter_0_LED,
  output Counter_1_LED,
  output Counter_2_LED,
  output Counter_3_LED,
  output Counter_4_LED,
  output Counter_5_LED,
  output Counter_6_LED,
  output Counter_7_LED,
  output Counter_8_LED,
  output Counter_9_LED,
  output Counter_10_LED,
  output Counter_11_LED,
  output Counter_12_LED,
  output Counter_13_LED,
  output Counter_14_LED,
  output Counter_15_LED,
  output [15:0] XFER_BUS_OUT,
  output LOAD_LED,
  output INC_LED,
  output DEC_LED,
  output [15:0] ADDR_BUS_OUT,
  output XFER_ASSERT_LED,
  output ADDR_ASSERT_LED
);

  wire or_1_out;
  wire [15:0] register_1_q;

  Counter #(.max('hffff), .width(16)) counter_1 (
    .clr(RST_IN), .load(LOAD), .up(INC), .count(1'b1), .clk(or_1_out), .D(XFER_BUS_IN),
    .Q({Counter_15_LED, Counter_14_LED, Counter_13_LED, Counter_12_LED, Counter_11_LED, Counter_10_LED, Counter_9_LED, Counter_8_LED, Counter_7_LED, Counter_6_LED, Counter_5_LED, Counter_4_LED, Counter_3_LED, Counter_2_LED, Counter_1_LED, Counter_0_LED}));  // open: carry
  or or_1 (or_1_out, INC, LOAD, DEC);
  Register #(.width(16)) register_1 (
    .D({Counter_15_LED, Counter_14_LED, Counter_13_LED, Counter_12_LED, Counter_11_LED, Counter_10_LED, Counter_9_LED, Counter_8_LED, Counter_7_LED, Counter_6_LED, Counter_5_LED, Counter_4_LED, Counter_3_LED, Counter_2_LED, Counter_1_LED, Counter_0_LED}),
    .en(1'b1), .clk(CLK_IN), .Q(register_1_q), .clr(RST_IN));
  assign XFER_BUS_OUT = XFER_ASSERT ? register_1_q : 16'bz;  // Controlled_Buffer controlled_buffer_1
  assign ADDR_BUS_OUT = ADDR_ASSERT ? register_1_q : 16'bz;  // Controlled_Buffer controlled_buffer_2

  assign ADDR_ASSERT_LED = ADDR_ASSERT;
  assign DEC_LED = DEC;
  assign INC_LED = INC;
  assign LOAD_LED = LOAD;
  assign XFER_ASSERT_LED = XFER_ASSERT;
endmodule

module Constant_Register (
  input  [7:0] MEM_BUS_IN,
  input  MEM_BUS_LOAD,
  input  DATA_ASSERT,
  input  RST_IN,
  input  [7:0] DATA_BUS_IN,
  input  DATA_BUS_LOAD,
  output Regsiter_0_LED,
  output Register_1_LED,
  output Register_2_LED,
  output Register_3_LED,
  output Register_4_LED,
  output Register_5_LED,
  output Register_6_LED,
  output Register_7_LED,
  output [7:0] DATA_BUS_OUT,
  output MEM_BUS_LOAD_LED,
  output DATA_ASSERT_LED,
  output DataBus_0_LED,
  output DataBus_1_LED,
  output DataBus_2_LED,
  output DataBus_3_LED,
  output DataBus_4_LED,
  output DataBus_5_LED,
  output DataBus_6_LED,
  output DataBus_7_LED
);

  wire nor_1_out, nor_2_out;
  wire [7:0] register_1_q, register_2_q;

  nor nor_1 (nor_1_out, MEM_BUS_LOAD, nor_2_out);
  nor nor_2 (nor_2_out, nor_1_out, DATA_BUS_LOAD);
  Register register_1 (.D(MEM_BUS_IN), .en(1'b1), .clk(MEM_BUS_LOAD), .Q(register_1_q), .clr(RST_IN));
  Register register_2 (.D(DATA_BUS_IN), .en(1'b1), .clk(DATA_BUS_LOAD), .Q(register_2_q), .clr(RST_IN));
  assign {Register_7_LED, Register_6_LED, Register_5_LED, Register_4_LED, Register_3_LED, Register_2_LED, Register_1_LED, Regsiter_0_LED} = nor_2_out ? register_1_q : 8'bz;  // Controlled_Buffer controlled_buffer_1
  assign {Register_7_LED, Register_6_LED, Register_5_LED, Register_4_LED, Register_3_LED, Register_2_LED, Register_1_LED, Regsiter_0_LED} = nor_1_out ? register_2_q : 8'bz;  // Controlled_Buffer controlled_buffer_2
  assign DATA_BUS_OUT = DATA_ASSERT ? {Register_7_LED, Register_6_LED, Register_5_LED, Register_4_LED, Register_3_LED, Register_2_LED, Register_1_LED, Regsiter_0_LED} : 8'bz;  // Controlled_Buffer controlled_buffer_3

  assign DATA_ASSERT_LED = DATA_ASSERT;
  assign DataBus_0_LED = DATA_BUS_IN[0];
  assign DataBus_1_LED = DATA_BUS_IN[1];
  assign DataBus_2_LED = DATA_BUS_IN[2];
  assign DataBus_3_LED = DATA_BUS_IN[3];
  assign DataBus_4_LED = DATA_BUS_IN[4];
  assign DataBus_5_LED = DATA_BUS_IN[5];
  assign DataBus_6_LED = DATA_BUS_IN[6];
  assign DataBus_7_LED = DATA_BUS_IN[7];
  assign MEM_BUS_LOAD_LED = MEM_BUS_LOAD;
endmodule

module Transfer_Register (
  input  [15:0] XFER_BUS_IN,
  input  TX_LOAD,
  input  TL_ASSERT,
  input  RST_IN,
  input  TX_XFER_ASSERT,
  input  [7:0] DATA_BUS_IN,
  input  TL_LOAD,
  input  TX_ADDR_ASSERT,
  input  TH_ASSERT,
  input  TH_LOAD,
  output Regsiter_0_LED,
  output Register_1_LED,
  output Register_2_LED,
  output Register_3_LED,
  output Register_4_LED,
  output Register_5_LED,
  output Register_6_LED,
  output Register_7_LED,
  output [7:0] DATA_BUS_OUT,
  output TX_LOAD_LED,
  output TL_ASSERT_LED,
  output TX_XFER_ASSERT_LED,
  output [15:0] XFER_BUS_OUT,
  output TL_LOAD_LED,
  output Register_8_LED,
  output [15:0] ADDR_BUS_OUT,
  output Register_9_LED,
  output Register_10_LED,
  output Register_11_LED,
  output TX_ADDR_ASSERT_LED,
  output Register_12_LED,
  output Register_13_LED,
  output Register_14_LED,
  output Register_15_LED,
  output TH_ASSERT_LED,
  output TH_LOAD_LED
);

  wire nor_1_out, nor_2_out, nor_3_out, nor_4_out;
  wire [7:0] register_1_q, register_2_q, register_3_q, register_4_q;

  nor nor_1 (nor_1_out, TX_LOAD, nor_2_out);
  nor nor_2 (nor_2_out, nor_1_out, TL_LOAD);
  nor nor_3 (nor_3_out, TX_LOAD, nor_4_out);
  nor nor_4 (nor_4_out, nor_3_out, TH_LOAD);
  Register register_1 (.D(XFER_BUS_IN[7:0]), .en(1'b1), .clk(TX_LOAD), .Q(register_1_q), .clr(RST_IN));
  Register register_2 (.D(DATA_BUS_IN), .en(1'b1), .clk(TL_LOAD), .Q(register_2_q), .clr(RST_IN));
  Register register_3 (.D(XFER_BUS_IN[15:8]), .en(1'b1), .clk(TX_LOAD), .Q(register_3_q), .clr(RST_IN));
  Register register_4 (.D(DATA_BUS_IN), .en(1'b1), .clk(TH_LOAD), .Q(register_4_q), .clr(RST_IN));
  assign {Register_7_LED, Register_6_LED, Register_5_LED, Register_4_LED, Register_3_LED, Register_2_LED, Register_1_LED, Regsiter_0_LED} = nor_2_out ? register_1_q : 8'bz;  // Controlled_Buffer controlled_buffer_1
  assign {Register_7_LED, Register_6_LED, Register_5_LED, Register_4_LED, Register_3_LED, Register_2_LED, Register_1_LED, Regsiter_0_LED} = nor_1_out ? register_2_q : 8'bz;  // Controlled_Buffer controlled_buffer_2
  assign {Register_15_LED, Register_14_LED, Register_13_LED, Register_12_LED, Register_11_LED, Register_10_LED, Register_9_LED, Register_8_LED} = nor_4_out ? register_3_q : 8'bz;  // Controlled_Buffer controlled_buffer_3
  assign {Register_15_LED, Register_14_LED, Register_13_LED, Register_12_LED, Register_11_LED, Register_10_LED, Register_9_LED, Register_8_LED} = nor_3_out ? register_4_q : 8'bz;  // Controlled_Buffer controlled_buffer_4
  assign DATA_BUS_OUT = TL_ASSERT ? {Register_7_LED, Register_6_LED, Register_5_LED, Register_4_LED, Register_3_LED, Register_2_LED, Register_1_LED, Regsiter_0_LED} : 8'bz;  // Controlled_Buffer controlled_buffer_5
  assign DATA_BUS_OUT = TH_ASSERT ? {Register_15_LED, Register_14_LED, Register_13_LED, Register_12_LED, Register_11_LED, Register_10_LED, Register_9_LED, Register_8_LED} : 8'bz;  // Controlled_Buffer controlled_buffer_6
  assign XFER_BUS_OUT = TX_XFER_ASSERT ? {Register_15_LED, Register_14_LED, Register_13_LED, Register_12_LED, Register_11_LED, Register_10_LED, Register_9_LED, Register_8_LED, Register_7_LED, Register_6_LED, Register_5_LED, Register_4_LED, Register_3_LED, Register_2_LED, Register_1_LED, Regsiter_0_LED} : 16'bz;  // Controlled_Buffer controlled_buffer_7
  assign ADDR_BUS_OUT = TX_ADDR_ASSERT ? {Register_15_LED, Register_14_LED, Register_13_LED, Register_12_LED, Register_11_LED, Register_10_LED, Register_9_LED, Register_8_LED, Register_7_LED, Register_6_LED, Register_5_LED, Register_4_LED, Register_3_LED, Register_2_LED, Register_1_LED, Regsiter_0_LED} : 16'bz;  // Controlled_Buffer controlled_buffer_8

  assign TH_ASSERT_LED = TH_ASSERT;
  assign TH_LOAD_LED = TH_LOAD;
  assign TL_ASSERT_LED = TL_ASSERT;
  assign TL_LOAD_LED = TL_LOAD;
  assign TX_ADDR_ASSERT_LED = TX_ADDR_ASSERT;
  assign TX_LOAD_LED = TX_LOAD;
  assign TX_XFER_ASSERT_LED = TX_XFER_ASSERT;
endmodule

module Bus_Control (
  input  RST_IN,
  input  CLK_IN,
  input  [25:0] CONTROL_IN,
  output A_RST,
  output B_RST,
  output C_RST,
  output D_RST,
  output CONST_RST,
  output PC_RST,
  output RA_RST,
  output PC_CLK,
  output SP_RST,
  output RA_CLK,
  output SI_RST,
  output SP_CLK,
  output DI_RST,
  output SI_CLK,
  output TX_RST,
  output DI_CLK,
  output A_LOAD,
  output SP_INC,
  output PC_INC,
  output B_LOAD,
  output SI_INC,
  output RA_INC,
  output CONST_MEM_LOAD,
  output PC_LOAD,
  output C_LOAD,
  output DI_INC,
  output PC_DEC,
  output RA_LOAD,
  output D_LOAD,
  output RA_DEC,
  output SP_LOAD,
  output CONST_DATA_LOAD,
  output SP_DEC,
  output SI_LOAD,
  output TL_LOAD,
  output SI_DEC,
  output DI_LOAD,
  output TH_LOAD,
  output A_RHS_ASSERT,
  output DI_DEC,
  output TX_LOAD,
  output A_LHS_ASSERT,
  output B_RHS_ASSERT,
  output [5:0] DEVICE_LOAD,
  output B_LHS_ASSERT,
  output C_RHS_ASSERT,
  output C_LHS_ASSERT,
  output D_RHS_ASSERT,
  output D_LHS_ASSERT,
  output PC_XFER_ASSERT,
  output RA_XFER_ASSERT,
  output PC_ADDR_ASSERT,
  output SP_XFER_ASSERT,
  output RA_ADDR_ASSERT,
  output SI_XFER_ASSERT,
  output SP_ADDR_ASSERT,
  output DI_XFER_ASSERT,
  output SI_ADDR_ASSERT,
  output TX_XFER_ASSERT,
  output DI_ADDR_ASSERT,
  output TX_MODE_ASSERT,
  output TX_ADDR_ASSERT,
  output A_DATA_ASSERT,
  output B_DATA_ASSERT,
  output C_DATA_ASSSERT,
  output D_DATA_ASSERT,
  output CONST_ASSERT,
  output TL_ASSERT,
  output TH_ASSERT,
  output ALU_ASSERT,
  output [5:0] DEVICE_ASSERT,
  output [3:0] MEM_CONTROL
);

  wire and_1_out, and_2_out, not_1_out, not_2_out;
  wire [0:0] decoder_3_out0, decoder_5_out0, decoder_8_out0;
  wire [3:2] decoder_10_out2;
  wire [7:0] decoder_6_out0;
  wire [7:6] decoder_4_out6;
  wire [7:7] decoder_7_out7;
  wire [8:0] decoder_1_out0;
  wire [14:0] decoder_2_out0;

  not not_1 (not_1_out, CLK_IN);
  Decoder #(.select(4)) decoder_1 (
    .out0(decoder_1_out0[0]), .out1(A_LOAD), .out2(B_LOAD), .out3(C_LOAD), .out4(D_LOAD),
    .out5(CONST_DATA_LOAD), .out6(TL_LOAD), .out7(TH_LOAD), .out8(decoder_1_out0[8]), .out9(DEVICE_LOAD[0]),
    .out10(DEVICE_LOAD[1]), .out11(DEVICE_LOAD[2]), .out12(DEVICE_LOAD[3]), .out13(DEVICE_LOAD[4]),
    .out14(DEVICE_LOAD[5]), .out15(MEM_CONTROL[2]), .sel(CONTROL_IN[21:18]), .en(not_1_out));
  Decoder #(.enable("false"), .select(4)) decoder_2 (
    .out0(decoder_2_out0[0]), .out1(decoder_2_out0[1]), .out2(decoder_2_out0[2]), .out3(decoder_2_out0[3]),
    .out4(decoder_2_out0[4]), .out5(decoder_2_out0[5]), .out6(decoder_2_out0[6]), .out7(decoder_2_out0[7]),
    .out8(decoder_2_out0[8]), .out9(decoder_2_out0[9]), .out10(decoder_2_out0[10]),
    .out11(decoder_2_out0[11]), .out12(decoder_2_out0[12]), .out13(decoder_2_out0[13]),
    .out14(decoder_2_out0[14]), .out15(MEM_CONTROL[1]), .sel(CONTROL_IN[21:18]));
  Decoder #(.enable("false"), .select(4)) decoder_3 (
    .out0(decoder_3_out0[0]), .out1(A_DATA_ASSERT), .out2(B_DATA_ASSERT), .out3(C_DATA_ASSSERT),
    .out4(D_DATA_ASSERT), .out5(CONST_ASSERT), .out6(TL_ASSERT), .out7(TH_ASSERT), .out8(ALU_ASSERT),
    .out9(DEVICE_ASSERT[0]), .out10(DEVICE_ASSERT[1]), .out11(DEVICE_ASSERT[2]), .out12(DEVICE_ASSERT[3]),
    .out13(DEVICE_ASSERT[4]), .out14(DEVICE_ASSERT[5]), .out15(MEM_CONTROL[3]), .sel(CONTROL_IN[25:22]));
  // LedBar #(.inputtype("row"), .matrixcols(16)) ledbar_1: pin names not known; wires that end beside it: {MEM_CONTROL[2], DEVICE_LOAD, decoder_1_out0[8], TH_LOAD, TL_LOAD, CONST_DATA_LOAD, D_LOAD, C_LOAD, B_LOAD, A_LOAD, decoder_1_out0[0]}
  // LedBar #(.inputtype("row"), .matrixcols(16)) ledbar_2: pin names not known; wires that end beside it: {MEM_CONTROL[1], decoder_2_out0}
  // LedBar #(.inputtype("row"), .matrixcols(16)) ledbar_3: pin names not known; wires that end beside it: {MEM_CONTROL[3], DEVICE_ASSERT, ALU_ASSERT, TH_ASSERT, TL_ASSERT, CONST_ASSERT, D_DATA_ASSERT, C_DATA_ASSSERT, B_DATA_ASSERT, A_DATA_ASSERT, decoder_3_out0[0]}
  and and_1 (and_1_out, CONTROL_IN[7], not_1_out);
  Decoder #(.select(3)) decoder_4 (
    .out0(CONST_MEM_LOAD), .out1(PC_DEC), .out2(RA_DEC), .out3(SP_DEC), .out4(SI_DEC), .out5(DI_DEC),
    .out6(decoder_4_out6[6]), .out7(decoder_4_out6[7]), .sel(CONTROL_IN[6:4]), .en(and_1_out));
  Decoder #(.enable("false"), .select(3)) decoder_5 (
    .out0(decoder_5_out0[0]), .out1(PC_XFER_ASSERT), .out2(RA_XFER_ASSERT), .out3(SP_XFER_ASSERT),
    .out4(SI_XFER_ASSERT), .out5(DI_XFER_ASSERT), .out6(TX_XFER_ASSERT), .out7(TX_MODE_ASSERT),
    .sel(CONTROL_IN[10:8]));
  // LedBar #(.inputtype("row")) ledbar_4: pin names not known; wires that end beside it: {decoder_4_out6, DI_DEC, SI_DEC, SP_DEC, RA_DEC, PC_DEC, CONST_MEM_LOAD}
  // LedBar #(.inputtype("row")) ledbar_5: pin names not known; wires that end beside it: {TX_MODE_ASSERT, TX_XFER_ASSERT, DI_XFER_ASSERT, SI_XFER_ASSERT, SP_XFER_ASSERT, RA_XFER_ASSERT, PC_XFER_ASSERT, decoder_5_out0[0]}
  not not_2 (not_2_out, CONTROL_IN[7]);
  and and_2 (and_2_out, not_2_out, not_1_out);
  Decoder #(.select(3)) decoder_6 (
    .out0(decoder_6_out0[0]), .out1(PC_LOAD), .out2(RA_LOAD), .out3(SP_LOAD), .out4(SI_LOAD), .out5(DI_LOAD),
    .out6(TX_LOAD), .out7(decoder_6_out0[7]), .sel(CONTROL_IN[6:4]), .en(and_2_out));
  Decoder #(.enable("false"), .select(3)) decoder_7 (
    .out0(MEM_CONTROL[0]), .out1(PC_ADDR_ASSERT), .out2(RA_ADDR_ASSERT), .out3(SP_ADDR_ASSERT),
    .out4(SI_ADDR_ASSERT), .out5(DI_ADDR_ASSERT), .out6(TX_ADDR_ASSERT), .out7(decoder_7_out7[7]),
    .sel(CONTROL_IN[13:11]));
  // LedBar #(.inputtype("row")) ledbar_6: pin names not known; wires that end beside it: {decoder_6_out0[7], TX_LOAD, DI_LOAD, SI_LOAD, SP_LOAD, RA_LOAD, PC_LOAD, decoder_6_out0[0]}
  // LedBar #(.inputtype("row")) ledbar_7: pin names not known; wires that end beside it: {decoder_7_out7[7], TX_ADDR_ASSERT, DI_ADDR_ASSERT, SI_ADDR_ASSERT, SP_ADDR_ASSERT, RA_ADDR_ASSERT, PC_ADDR_ASSERT, MEM_CONTROL[0]}
  Decoder #(.select(2)) decoder_8 (
    .out0(decoder_8_out0[0]), .out1(SP_INC), .out2(SI_INC), .out3(DI_INC), .sel(CONTROL_IN[3:2]),
    .en(not_1_out));
  Decoder #(.enable("false"), .select(2)) decoder_9 (
    .out0(A_LHS_ASSERT), .out1(B_LHS_ASSERT), .out2(C_LHS_ASSERT), .out3(D_LHS_ASSERT),
    .sel(CONTROL_IN[17:16]));
  // LedBar #(.inputtype("row"), .matrixcols(4)) ledbar_8: pin names not known; wires that end beside it: {DI_INC, SI_INC, SP_INC, decoder_8_out0[0]}
  // LedBar #(.inputtype("row"), .matrixcols(4)) ledbar_9: pin names not known; wires that end beside it: {D_LHS_ASSERT, C_LHS_ASSERT, B_LHS_ASSERT, A_LHS_ASSERT}
  Decoder #(.select(2)) decoder_10 (
    .out0(PC_INC), .out1(RA_INC), .out2(decoder_10_out2[2]), .out3(decoder_10_out2[3]),
    .sel(CONTROL_IN[1:0]), .en(not_1_out));
  Decoder #(.enable("false"), .select(2)) decoder_11 (
    .out0(A_RHS_ASSERT), .out1(B_RHS_ASSERT), .out2(C_RHS_ASSERT), .out3(D_RHS_ASSERT),
    .sel(CONTROL_IN[15:14]));
  // LedBar #(.inputtype("row"), .matrixcols(4)) ledbar_10: pin names not known; wires that end beside it: {decoder_10_out2, RA_INC, PC_INC}
  // LedBar #(.inputtype("row"), .matrixcols(4)) ledbar_11: pin names not known; wires that end beside it: {D_RHS_ASSERT, C_RHS_ASSERT, B_RHS_ASSERT, A_RHS_ASSERT}

  assign A_RST = RST_IN;
  assign B_RST = RST_IN;
  assign C_RST = RST_IN;
  assign CONST_RST = RST_IN;
  assign D_RST = RST_IN;
  assign DI_CLK = CLK_IN;
  assign DI_RST = RST_IN;
  assign PC_CLK = CLK_IN;
  assign PC_RST = RST_IN;
  assign RA_CLK = CLK_IN;
  assign RA_RST = RST_IN;
  assign SI_CLK = CLK_IN;
  assign SI_RST = RST_IN;
  assign SP_CLK = CLK_IN;
  assign SP_RST = RST_IN;
  assign TX_RST = RST_IN;
endmodule
